// Logisim project apu.circ as structural Verilog
module BuzzerStress (
  input  in_1
);

  wire clock_1_out;
  wire [13:0] counter_1_q, rom_1_data;

  Clock clock_1 (.out(clock_1_out));
  Counter #(.max('h3fff), .width(14)) counter_1 (
    .count(1'b1), .clk(clock_1_out), .Q(counter_1_q));  // open: clr, load, up, D, carry
  ROM #(.addrWidth(11), .dataWidth(14)) rom_1 (.addr(counter_1_q[13:3]), .data(rom_1_data));
  // Buzzer #(.waveform("Square")) buzzer_1: pin names not known; wires that end beside it: rom_1_data, in_1, 7'b1000000

  // Notes on the sheet:
  //   contents of rom_1 (hex, n*v repeats v):
  //   6*3fff 3e6c 369f 308d 2bb2 27b9 246a 219d 1f36 1d21 1b4f 19b4 1846 16ff 15d9 14cf 13dd 1300 1235
  //   117a 10ce 102f f9b f11 e91 e18 da8 d3e cda c7c c23 bcf b80 b34 aed aa8 a67 a29 9ee 9b6 980 94c 91a
  //   8eb 8bd 891 867 83f 817 7f2 7ce 7aa 789 768 748 72a 70c 6f0 6d4 6b9 69f 686 66d 655 63e 628 612 5fc
  //   5e8 5d3 5c0 5ad 59a 588 576 565 554 544 534 524 515 506 4f7 4e9 4db 4cd 4c0 4b3 4a6 499 48d 481 475
  //   46a 45f 454 449 43e 434 429 41f 415 40c 402 3f9 3f0 3e7 3de 3d5 3cd 3c4 3bc 3b4 3ac 3a4 39c 395 38d
  //   386 37f 378 371 36a 363 35c 356 34f 349 343 33d 337 331 32b 325 31f 319 314 30e 309 303 2fe 2f9 2f4
  //   2ef 2ea 2e5 2e0 2db 2d6 2d2 2cd 2c8 2c4 2c0 2bb 2b7 2b2 2ae 2aa 2a6 2a2 29e 29a 296 292 28e 28a 287
  //   283 27f 27c 278 274 271 26d 26a 267 263 260 25d 259 256 253 250 24d 24a 247 244 241 23e 23b 238 235
  //   232 22f 22d 22a 227 224 222 21f 21c 21a 217 215 212 210 20d 20b 208 206 203 201 1ff 1fc 1fa 1f8 1f6
  //   1f3 1f1 1ef 1ed 1eb 1e8 1e6 1e4 1e2 1e0 1de 1dc 1da 1d8 1d6 1d4 1d2 1d0 1ce 1cc 1ca 1c9 1c7 1c5 1c3
  //   1c1 1bf 1be 1bc 1ba 1b8 1b7 1b5 1b3 1b2 1b0 1ae 1ad 1ab 1a9 1a8 1a6 1a5 1a3 1a1 1a0 19e 19d 19b 19a
  //   198 197 195 194 192 191 190 18e 18d 18b 18a 188 187 186 184 183 182 180 17f 17e 17c 17b 17a 179 177
  //   176 175 174 172 171 170 16f 16e 16c 16b 16a 169 168 167 165 164 163 162 161 160 15f 15e 15c 15b 15a
  //   159 158 157 156 155 154 153 152 151 150 14f 14e 14d 14c 14b 14a 149 148 147 146 145 144 143 142 141
  //   141 140 13f 13e 13d 13c 13b 13a 139 138 138 137 136 135 134 133 132 132 131 130 12f 12e 12e 12d 12c
  //   12b 12a 12a 129 128 127 126 126 125 124 123 123 122 121 120 120 11f 11e 11d 11d 11c 11b 11a 11a 119
  //   118 118 117 116 116 115 114 114 113 112 111 111 110 110 10f 10e 10e 10d 10c 10c 10b 10a 10a 109 108
  //   108 107 107 106 105 105 104 104 103 102 102 101 101 100 ff ff fe fe fd fd fc fb fb fa fa f9 f9 f8 f7
  //   f7 f6 f6 f5 f5 f4 f4 f3 f3 f2 f2 f1 f1 f0 f0 ef ef ee ed ed ec ec eb eb eb ea ea e9 e9 e8 e8 e7 e7
  //   e6 e6 e5 e5 e4 e4 e3 e3 e2 e2 e2 e1 e1 e0 e0 df df de de de dd dd dc dc db db da da da d9 d9 d8 d8
  //   d8 d7 d7 d6 d6 d5 d5 d5 d4 d4 d3 d3 d3 d2 d2 d1 d1 d1 d0 d0 d0 cf cf ce ce ce cd cd cc cc cc cb cb
  //   cb ca ca ca c9 c9 c8 c8 c8 c7 c7 c7 c6 c6 c6 c5 c5 c5 c4 c4 c4 c3 c3 c3 c2 c2 c2 c1 c1 c1 c0 c0 c0
  //   bf bf bf be be be bd bd bd bc bc bc bb bb bb 4*ba b9 b9 b9 b8 b8 b8 b7 b7 b7 4*b6 b5 b5 b5 4*b4 b3
  //   b3 b3 4*b2 b1 b1 b1 4*b0 4*af ae ae ae 4*ad 4*ac 4*ab aa aa aa 4*a9 4*a8 4*a7 4*a6 5*a5 4*a4 4*a3
  //   4*a2 4*a1 5*a0 4*9f 5*9e 4*9d 5*9c 5*9b 4*9a 5*99 5*98 5*97 5*96 5*95 5*94 5*93 5*92 6*91 5*90 5*8f
  //   6*8e 6*8d 5*8c 6*8b 6*8a 6*89 6*88 6*87 6*86 7*85 6*84 7*83 6*82 7*81 7*80 7*7f 7*7e 7*7d 7*7c 8*7b
  //   7*7a 8*79 8*78 7*77 9*76 8*75 8*74 8*73 9*72 9*71 9*70 9*6f 9*6e 9*6d 10*6c 10*6b 10*6a 10*69 10*68
  //   11*67 11*66 11*65 11*64 11*63 12*62 12*61 12*60 12*5f 13*5e 13*5d 13*5c 14*5b 13*5a 14*59 15*58
  //   15*57 15*56 15*55 16*54 16*53 17*52 17*51 18*50 17*4f 19*4e 19*4d 19*4c 20*4b 20*4a 21*49 22*48
  //   22*47 23*46 24*45 24*44 25*43 25*42 27*41 27*40 28*3f 29*3e 30*3d 32*3c 32*3b 33*3a 34*39 36*38
  //   33*37
endmodule

module RegFile (
  input  WR,
  input  [3:0] reg_id,
  input  [7:0] value,
  output [7:0] reg0_out,
  output [7:0] reg2_out,
  output [7:0] reg3_out,
  output [7:0] reg9_out
);

  Decoder #(.enable("false"), .select(4)) decoder_1 (.sel(reg_id));  // open: out0, out1, out2, out3, out4, out5, out6, out7, out8, out9, out10, out11, out12, out13, out14, out15
  Register reg0 (.D(value), .clk(WR), .Q(reg0_out), .clr(1'b0));  // open: en
  Register reg2 (.D(value), .clk(WR), .Q(reg2_out), .clr(1'b0));  // open: en
  Register reg3 (.D(value), .clk(WR), .Q(reg3_out), .clr(1'b0));  // open: en
  Register reg9 (.D(value), .clk(WR), .Q(reg9_out), .clr(1'b0));  // open: en
endmodule
