// Logisim project apu.circ as structural Verilog
module apu_test (
  input  [3:0] in_1,
  input  [7:0] in_2,
  input  pulse1,
  input  pulse2,
  input  triangle,
  input  noise,
  output out_7
);

  wire and_1_out, button_1_out, clock_1_out, counter_2_carry, wr_test_out;
  wire [15:0] counter_1_q, rom_1_data;

  Clock clock_1 (.out(clock_1_out));
  Button button_1 (.out(button_1_out));
  Counter #(.max('hffff), .width(16)) counter_1 (
    .clr(button_1_out), .up(1'b1), .count(1'b1), .clk(clock_1_out), .Q(counter_1_q));  // open: load, D, carry
  ROM #(.addrWidth(16), .dataWidth(16)) rom_1 (.addr(counter_1_q), .data({rom_1_data[15:13], out_7, rom_1_data[11:0]}));
  and and_1 (and_1_out, clock_1_out, out_7);
  Button wr_test (.out(wr_test_out));
  APU apu_1 (
    .ch_mask({noise, triangle, pulse2, pulse1}), .WR(and_1_out), .reg_id(rom_1_data[11:8]),
    .value(rom_1_data[7:0]), .frame_clk(counter_2_carry));
  Counter #(.max('h1f)) counter_2 (.clk(clock_1_out), .carry(counter_2_carry));  // open: clr, load, up, count, D, Q

  // Notes on the sheet:
  //   pulse1: initial=0x1
  //   pulse2: initial=0x1
  //   triangle: initial=0x1
  //   noise: initial=0x1
  //   contents of rom_1 (hex, n*v repeats v):
  //   1b00 1a00 1800 1700 1600 1500 1400 1300 1200 1100 1f00 1e00 1c30 190f 1108 1508 16*0 1030 143a 1696
  //   1708 28*0 1478 31*0 14b8 159*0 14b6 223*0 14b5 223*0 14b4 223*0 103a 12bd 1308 14b3 28*0 1078 31*0
  //   10b8 159*0 10b6 14b2 222*0 10b5 14b1 222*0 10b4 223*0 10b3 1430 222*0 10b2 223*0 10b1 447*0 1030
  //   895*0 1c3c 1e0b 1f08 29*0 1c36 31*0 1c31 31*0 1c30 799*0 1c3c 31*0 1c36 31*0 1c31 31*0 1c30 799*0
  //   1c3c 31*0 1c36 31*0 1c31 31*0 1c30 351*0 143c 161c 1709 29*0 143a 160c 30*0 16fd 1708 126*0 1430
  //   31*0 1434 161c 1709 29*0 160c 31*0 16fd 1708 126*0 1430 31*0 143c 161c 1709 1c3c 28*0 143a 1c36 30*0
  //   1c31 31*0 1c30 95*0 1430 31*0 143c 163f 30*0 143a 159*0 1430 31*0 143c 16ab 30*0 143a 319*0 1693
  //   63*0 1430 1c31 30*0 1077 12bf 130b 143c 167c 18ff 1a3f 1b09 1c3c 23*0 143a 1adf 1c36 29*0 1c31 31*0
  //   1c30 351*0 1030 1430 1800 221*0 1434 191*0 1430 31*0 1072 143c 161c 18ff 1a3f 1c3c 26*0 143a 160c
  //   1adf 1c36 28*0 16fd 1708 1800 1c31 28*0 1c30 127*0 1430 223*0 1077 1434 161c 1709 18ff 27*0 160c
  //   31*0 16fd 1708 126*0 1430 31*0 143c 161c 1709 29*0 143a 159*0 1030 1800 30*0 1077 12f8 1430 18ff
  //   1a52 1c3c 26*0 1afb 1c36 30*0 1c31 31*0 1c30 127*0 143c 167c 30*0 143a 159*0 1430 31*0 1030 143c
  //   1800 29*0 143a 159*0 1430 31*0 1077 143c 18ff 29*0 143a 159*0 1430 31*0 1434 1a52 1c3c 29*0 1afb
  //   1c36 30*0 1c31 31*0 1c30 95*0 1430 31*0 1030 143c 1800 29*0 143a 159*0 1430 31*0 1077 12f3 130d 143c
  //   16ab 18ff 1af9 1b0a 24*0 143a 383*0 1430 31*0 1030 143c 167c 1afb 1b09 1c3c 26*0 143a 1af9 1b0a 1c36
  //   28*0 1800 1c31 30*0 1c30 95*0 1430 31*0 1434 191*0 1430 31*0 1077 143c 18ff 29*0 143a 159*0 1430
  //   31*0 1434 191*0 1430 31*0 1030 143c 161c 1afb 1b09 1c3c 26*0 143a 160c 1af9 1b0a 1c36 27*0 16fd 1708
  //   1800 1c31 28*0 1c30 351*0 1072 31*0 16ef 95*0 16fd 63*0 1430 31*0 143c 161c 1709 29*0 143a 191*0
  //   1030 1430 18ff 1afb 1b09 1c3c 26*0 1af9 1b0a 1c36 29*0 1800 1c31 30*0 1c30 127*0 1434 191*0 1430
  //   31*0 1071 143c 162d 29*0 143a 161c 30*0 160c 127*0 1430 31*0 1434 191*0 1430 31*0 1077 12f8 130b
  //   143c 161c 18ff 1a52 1b09 1c3c 23*0 143a 1afb 1c36 29*0 1c31 31*0 1c30 95*0 1430 31*0 143c 163f 30*0
  //   143a 159*0 1430 31*0 143c 31*0 143a 383*0 1030 1430 1800 29*0 1077 12bf 1434 18ff 1a3f 1c3c 26*0
  //   1adf 1c36 30*0 1c31 31*0 1c30 95*0 1430 31*0 143c 16ab 30*0 143a 159*0 1430 31*0 1030 143c 167c 1800
  //   28*0 143a 159*0 1430 31*0 1434 191*0 1430 31*0 1072 143c 16ab 18ff 1a3f 1c3c 26*0 143a 1adf 1c36
  //   29*0 1800 1c31 30*0 1c30 95*0 1430 31*0 143c 167c 30*0 143a 159*0 1430 31*0 1077 1434 18ff 189*0
  //   1430 31*0 143c 161c 30*0 143a 159*0 1030 1800 30*0 1077 12f8 18ff 1a52 1c3c 27*0 1afb 1c36 30*0 1c31
  //   31*0 1c30 95*0 1430 31*0 143c 31*0 143a 159*0 1430 31*0 1030 143c 160c 1800 28*0 143a 159*0 1430
  //   31*0 1077 143c 16fd 1708 18ff 27*0 143a 159*0 1430 31*0 1434 1a52 1c3c 29*0 1afb 1c36 30*0 1c31 31*0
  //   1c30 95*0 1430 31*0 1030 143c 16ab 1709 1800 27*0 143a 159*0 1430 31*0 1077 12f3 130d 143c 18ff 1af9
  //   1b0a 25*0 143a 159*0 1430 31*0 143c 31*0 143a 159*0 1430 31*0 1030 143c 1afb 1b09 1c3c 27*0 143a
  //   1af9 1b0a 1c36 28*0 1800 1c31 30*0 1c30 95*0 1430 31*0 143c 31*0 143a 159*0 1430 31*0 1077 143c 18ff
  //   29*0 143a 159*0 1430 31*0 143c 31*0 143a 159*0 1430 31*0 1030 143c 1afb 1b09 1c3c 27*0 143a 1af9
  //   1b0a 1c36 28*0 1800 1c31 30*0 1c30 319*0 1430 31*0 1072 143c 1693 29*0 143a 159*0 1430 31*0 143c
  //   167c 30*0 143a 191*0 1030 1430 18ff 1afb 1b09 1c3c 26*0 1af9 1b0a 1c36 29*0 1800 1c31 30*0 1c30
  //   127*0 1434 191*0 1430 31*0 1071 143c 161c 29*0 143a 160c 30*0 16fd 1708 126*0 1430 31*0 1434 191*0
  //   1430 31*0 1077 12f8 130b 143c 161c 1709 18ff 1a52 1b09 1c3c 22*0 143a 1afb 1c36 29*0 1c31 31*0 1c30
  //   95*0 1430 31*0 143c 163f 30*0 143a 159*0 1430 31*0 143c 16ab 30*0 143a 319*0 1693 63*0 1030 1430
  //   1800 29*0 1077 12bf 143c 167c 18ff 1a3f 1c3c 25*0 143a 1adf 1c36 29*0 1c31 31*0 1c30 351*0 1030 1430
  //   1800 221*0 1434 191*0 1430 31*0 1072 143c 161c 18ff 1a3f 1c3c 26*0 143a 160c 1adf 1c36 28*0 16fd
  //   1708 1800 1c31 28*0 1c30 127*0 1430 223*0 1077 1434 161c 1709 18ff 27*0 160c 31*0 16fd 1708 126*0
  //   1430 31*0 143c 161c 1709 29*0 143a 159*0 1030 1800 30*0 1077 1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
endmodule

module BuzzerStress (
  input  in_1
);

  wire undriven;
  wire [13:0] counter_1_q, rom_1_data;

  Counter #(.max('h3fff), .width(14)) counter_1 (
    .count(1'b1), .clk(undriven), .Q(counter_1_q));  // open: clr, load, up, D, carry
  ROM #(.addrWidth(11), .dataWidth(14)) rom_1 (.addr(counter_1_q[13:3]), .data(rom_1_data));
  // Buzzer #(.waveform("Square")) buzzer_1: pin names not known; wires that end beside it: rom_1_data, in_1, 7'b1000000

  // Notes on the sheet:
  //   contents of rom_1 (hex, n*v repeats v):
  //   6*3fff 3e6c 369f 308d 2bb2 27b9 246a 219d 1f36 1d21 1b4f 19b4 1846 16ff 15d9 14cf 13dd 1300 1235
  //   117a 10ce 102f f9b f11 e91 e18 da8 d3e cda c7c c23 bcf b80 b34 aed aa8 a67 a29 9ee 9b6 980 94c 91a
  //   8eb 8bd 891 867 83f 817 7f2 7ce 7aa 789 768 748 72a 70c 6f0 6d4 6b9 69f 686 66d 655 63e 628 612 5fc
  //   5e8 5d3 5c0 5ad 59a 588 576 565 554 544 534 524 515 506 4f7 4e9 4db 4cd 4c0 4b3 4a6 499 48d 481 475
  //   46a 45f 454 449 43e 434 429 41f 415 40c 402 3f9 3f0 3e7 3de 3d5 3cd 3c4 3bc 3b4 3ac 3a4 39c 395 38d
  //   386 37f 378 371 36a 363 35c 356 34f 349 343 33d 337 331 32b 325 31f 319 314 30e 309 303 2fe 2f9 2f4
  //   2ef 2ea 2e5 2e0 2db 2d6 2d2 2cd 2c8 2c4 2c0 2bb 2b7 2b2 2ae 2aa 2a6 2a2 29e 29a 296 292 28e 28a 287
  //   283 27f 27c 278 274 271 26d 26a 267 263 260 25d 259 256 253 250 24d 24a 247 244 241 23e 23b 238 235
  //   232 22f 22d 22a 227 224 222 21f 21c 21a 217 215 212 210 20d 20b 208 206 203 201 1ff 1fc 1fa 1f8 1f6
  //   1f3 1f1 1ef 1ed 1eb 1e8 1e6 1e4 1e2 1e0 1de 1dc 1da 1d8 1d6 1d4 1d2 1d0 1ce 1cc 1ca 1c9 1c7 1c5 1c3
  //   1c1 1bf 1be 1bc 1ba 1b8 1b7 1b5 1b3 1b2 1b0 1ae 1ad 1ab 1a9 1a8 1a6 1a5 1a3 1a1 1a0 19e 19d 19b 19a
  //   198 197 195 194 192 191 190 18e 18d 18b 18a 188 187 186 184 183 182 180 17f 17e 17c 17b 17a 179 177
  //   176 175 174 172 171 170 16f 16e 16c 16b 16a 169 168 167 165 164 163 162 161 160 15f 15e 15c 15b 15a
  //   159 158 157 156 155 154 153 152 151 150 14f 14e 14d 14c 14b 14a 149 148 147 146 145 144 143 142 141
  //   141 140 13f 13e 13d 13c 13b 13a 139 138 138 137 136 135 134 133 132 132 131 130 12f 12e 12e 12d 12c
  //   12b 12a 12a 129 128 127 126 126 125 124 123 123 122 121 120 120 11f 11e 11d 11d 11c 11b 11a 11a 119
  //   118 118 117 116 116 115 114 114 113 112 111 111 110 110 10f 10e 10e 10d 10c 10c 10b 10a 10a 109 108
  //   108 107 107 106 105 105 104 104 103 102 102 101 101 100 ff ff fe fe fd fd fc fb fb fa fa f9 f9 f8 f7
  //   f7 f6 f6 f5 f5 f4 f4 f3 f3 f2 f2 f1 f1 f0 f0 ef ef ee ed ed ec ec eb eb eb ea ea e9 e9 e8 e8 e7 e7
  //   e6 e6 e5 e5 e4 e4 e3 e3 e2 e2 e2 e1 e1 e0 e0 df df de de de dd dd dc dc db db da da da d9 d9 d8 d8
  //   d8 d7 d7 d6 d6 d5 d5 d5 d4 d4 d3 d3 d3 d2 d2 d1 d1 d1 d0 d0 d0 cf cf ce ce ce cd cd cc cc cc cb cb
  //   cb ca ca ca c9 c9 c8 c8 c8 c7 c7 c7 c6 c6 c6 c5 c5 c5 c4 c4 c4 c3 c3 c3 c2 c2 c2 c1 c1 c1 c0 c0 c0
  //   bf bf bf be be be bd bd bd bc bc bc bb bb bb 4*ba b9 b9 b9 b8 b8 b8 b7 b7 b7 4*b6 b5 b5 b5 4*b4 b3
  //   b3 b3 4*b2 b1 b1 b1 4*b0 4*af ae ae ae 4*ad 4*ac 4*ab aa aa aa 4*a9 4*a8 4*a7 4*a6 5*a5 4*a4 4*a3
  //   4*a2 4*a1 5*a0 4*9f 5*9e 4*9d 5*9c 5*9b 4*9a 5*99 5*98 5*97 5*96 5*95 5*94 5*93 5*92 6*91 5*90 5*8f
  //   6*8e 6*8d 5*8c 6*8b 6*8a 6*89 6*88 6*87 6*86 7*85 6*84 7*83 6*82 7*81 7*80 7*7f 7*7e 7*7d 7*7c 8*7b
  //   7*7a 8*79 8*78 7*77 9*76 8*75 8*74 8*73 9*72 9*71 9*70 9*6f 9*6e 9*6d 10*6c 10*6b 10*6a 10*69 10*68
  //   11*67 11*66 11*65 11*64 11*63 12*62 12*61 12*60 12*5f 13*5e 13*5d 13*5c 14*5b 13*5a 14*59 15*58
  //   15*57 15*56 15*55 16*54 16*53 17*52 17*51 18*50 17*4f 19*4e 19*4d 19*4c 20*4b 20*4a 21*49 22*48
  //   22*47 23*46 24*45 24*44 25*43 25*42 27*41 27*40 28*3f 29*3e 30*3d 32*3c 32*3b 33*3a 34*39 36*38
  //   33*37
endmodule

module RegFile (
  input  WR,
  input  [3:0] reg_id,
  input  [7:0] value,
  output [7:0] reg0_out,
  output [7:0] reg2_out,
  output [7:0] reg3_out,
  output [7:0] reg9_out,
  output [7:0] reg12_out,
  output [7:0] reg4_out,
  output [7:0] reg10_out,
  output [7:0] reg6_out,
  output [7:0] reg14_out,
  output [7:0] reg11_out,
  output [7:0] reg7_out
);

  wire decoder_1_out0, decoder_1_out2, decoder_1_out3, decoder_1_out4, decoder_1_out6, decoder_1_out7,
       decoder_1_out9, decoder_1_out10, decoder_1_out11, decoder_1_out12, decoder_1_out14;

  Decoder #(.enable("false"), .select(4)) decoder_1 (
    .out0(decoder_1_out0), .out2(decoder_1_out2), .out3(decoder_1_out3), .out4(decoder_1_out4),
    .out6(decoder_1_out6), .out7(decoder_1_out7), .out9(decoder_1_out9), .out10(decoder_1_out10),
    .out11(decoder_1_out11), .out12(decoder_1_out12), .out14(decoder_1_out14), .sel(reg_id));  // open: out1, out5, out8, out13, out15
  Register reg0 (.D(value), .en(decoder_1_out0), .clk(WR), .Q(reg0_out), .clr(1'b0));
  Register reg2 (.D(value), .en(decoder_1_out2), .clk(WR), .Q(reg2_out), .clr(1'b0));
  Register reg3 (.D(value), .en(decoder_1_out3), .clk(WR), .Q(reg3_out), .clr(1'b0));
  Register reg9 (.D(value), .en(decoder_1_out9), .clk(WR), .Q(reg9_out), .clr(1'b0));
  Register reg4 (.D(value), .en(decoder_1_out4), .clk(WR), .Q(reg4_out), .clr(1'b0));
  Register reg6 (.D(value), .en(decoder_1_out6), .clk(WR), .Q(reg6_out), .clr(1'b0));
  Register reg7 (.D(value), .en(decoder_1_out7), .clk(WR), .Q(reg7_out), .clr(1'b0));
  Register reg10 (.D(value), .en(decoder_1_out10), .clk(WR), .Q(reg10_out), .clr(1'b0));
  Register reg11 (.D(value), .en(decoder_1_out11), .clk(WR), .Q(reg11_out), .clr(1'b0));
  Register reg12 (.D(value), .en(decoder_1_out12), .clk(WR), .Q(reg12_out), .clr(1'b0));
  Register reg14 (.D(value), .en(decoder_1_out14), .clk(WR), .Q(reg14_out), .clr(1'b0));
endmodule

module Channel_Pulse (
  input  enable,
  input  [7:0] reg0,
  input  [7:0] reg2,
  input  [7:0] reg3,
  input  frame_clk
);

  wire buzzer_1_p3;
  wire [3:0] VOL_q;
  wire [7:0] PW_q, rom_1_data;
  wire [13:0] freq_pulse_data, FREQ_q;

  ROM #(.addrWidth(11), .dataWidth(14)) freq_pulse (.addr({reg3[2:0], reg2}), .data(freq_pulse_data));
  ROM #(.addrWidth(2)) rom_1 (.addr(reg0[7:6]), .data(rom_1_data));
  Register #(.width(4)) VOL (.D(reg0[3:0]), .en(1'b1), .clk(frame_clk), .Q(VOL_q), .clr(1'b0));
  Register PW (.D(rom_1_data), .en(1'b1), .clk(frame_clk), .Q(PW_q), .clr(1'b0));
  Register #(.width(14)) FREQ (.D(freq_pulse_data), .en(1'b1), .clk(frame_clk), .Q(FREQ_q), .clr(1'b0));
  // Buzzer #(.vol_width(4), .waveform("Square")) buzzer_1: pin names not known; wires that end beside it: PW_q, FREQ_q, buzzer_1_p3, VOL_q
  Register #(.width(1)) ENABLE_R (.D(enable), .en(1'b1), .clk(frame_clk), .Q(buzzer_1_p3), .clr(1'b0));

  // Notes on the sheet:
  //   contents of freq_pulse (hex, n*v repeats v):
  //   6*3fff 3e6c 369f 308d 2bb2 27b9 246a 219d 1f36 1d21 1b4f 19b4 1846 16ff 15d9 14cf 13dd 1300 1235
  //   117a 10ce 102f f9b f11 e91 e18 da8 d3e cda c7c c23 bcf b80 b34 aed aa8 a67 a29 9ee 9b6 980 94c 91a
  //   8eb 8bd 891 867 83f 817 7f2 7ce 7aa 789 768 748 72a 70c 6f0 6d4 6b9 69f 686 66d 655 63e 628 612 5fc
  //   5e8 5d3 5c0 5ad 59a 588 576 565 554 544 534 524 515 506 4f7 4e9 4db 4cd 4c0 4b3 4a6 499 48d 481 475
  //   46a 45f 454 449 43e 434 429 41f 415 40c 402 3f9 3f0 3e7 3de 3d5 3cd 3c4 3bc 3b4 3ac 3a4 39c 395 38d
  //   386 37f 378 371 36a 363 35c 356 34f 349 343 33d 337 331 32b 325 31f 319 314 30e 309 303 2fe 2f9 2f4
  //   2ef 2ea 2e5 2e0 2db 2d6 2d2 2cd 2c8 2c4 2c0 2bb 2b7 2b2 2ae 2aa 2a6 2a2 29e 29a 296 292 28e 28a 287
  //   283 27f 27c 278 274 271 26d 26a 267 263 260 25d 259 256 253 250 24d 24a 247 244 241 23e 23b 238 235
  //   232 22f 22d 22a 227 224 222 21f 21c 21a 217 215 212 210 20d 20b 208 206 203 201 1ff 1fc 1fa 1f8 1f6
  //   1f3 1f1 1ef 1ed 1eb 1e8 1e6 1e4 1e2 1e0 1de 1dc 1da 1d8 1d6 1d4 1d2 1d0 1ce 1cc 1ca 1c9 1c7 1c5 1c3
  //   1c1 1bf 1be 1bc 1ba 1b8 1b7 1b5 1b3 1b2 1b0 1ae 1ad 1ab 1a9 1a8 1a6 1a5 1a3 1a1 1a0 19e 19d 19b 19a
  //   198 197 195 194 192 191 190 18e 18d 18b 18a 188 187 186 184 183 182 180 17f 17e 17c 17b 17a 179 177
  //   176 175 174 172 171 170 16f 16e 16c 16b 16a 169 168 167 165 164 163 162 161 160 15f 15e 15c 15b 15a
  //   159 158 157 156 155 154 153 152 151 150 14f 14e 14d 14c 14b 14a 149 148 147 146 145 144 143 142 141
  //   141 140 13f 13e 13d 13c 13b 13a 139 138 138 137 136 135 134 133 132 132 131 130 12f 12e 12e 12d 12c
  //   12b 12a 12a 129 128 127 126 126 125 124 123 123 122 121 120 120 11f 11e 11d 11d 11c 11b 11a 11a 119
  //   118 118 117 116 116 115 114 114 113 112 111 111 110 110 10f 10e 10e 10d 10c 10c 10b 10a 10a 109 108
  //   108 107 107 106 105 105 104 104 103 102 102 101 101 100 ff ff fe fe fd fd fc fb fb fa fa f9 f9 f8 f7
  //   f7 f6 f6 f5 f5 f4 f4 f3 f3 f2 f2 f1 f1 f0 f0 ef ef ee ed ed ec ec eb eb eb ea ea e9 e9 e8 e8 e7 e7
  //   e6 e6 e5 e5 e4 e4 e3 e3 e2 e2 e2 e1 e1 e0 e0 df df de de de dd dd dc dc db db da da da d9 d9 d8 d8
  //   d8 d7 d7 d6 d6 d5 d5 d5 d4 d4 d3 d3 d3 d2 d2 d1 d1 d1 d0 d0 d0 cf cf ce ce ce cd cd cc cc cc cb cb
  //   cb ca ca ca c9 c9 c8 c8 c8 c7 c7 c7 c6 c6 c6 c5 c5 c5 c4 c4 c4 c3 c3 c3 c2 c2 c2 c1 c1 c1 c0 c0 c0
  //   bf bf bf be be be bd bd bd bc bc bc bb bb bb 4*ba b9 b9 b9 b8 b8 b8 b7 b7 b7 4*b6 b5 b5 b5 4*b4 b3
  //   b3 b3 4*b2 b1 b1 b1 4*b0 4*af ae ae ae 4*ad 4*ac 4*ab aa aa aa 4*a9 4*a8 4*a7 4*a6 5*a5 4*a4 4*a3
  //   4*a2 4*a1 5*a0 4*9f 5*9e 4*9d 5*9c 5*9b 4*9a 5*99 5*98 5*97 5*96 5*95 5*94 5*93 5*92 6*91 5*90 5*8f
  //   6*8e 6*8d 5*8c 6*8b 6*8a 6*89 6*88 6*87 6*86 7*85 6*84 7*83 6*82 7*81 7*80 7*7f 7*7e 7*7d 7*7c 8*7b
  //   7*7a 8*79 8*78 7*77 9*76 8*75 8*74 8*73 9*72 9*71 9*70 9*6f 9*6e 9*6d 10*6c 10*6b 10*6a 10*69 10*68
  //   11*67 11*66 11*65 11*64 11*63 12*62 12*61 12*60 12*5f 13*5e 13*5d 13*5c 14*5b 13*5a 14*59 15*58
  //   15*57 15*56 15*55 16*54 16*53 17*52 17*51 18*50 17*4f 19*4e 19*4d 19*4c 20*4b 20*4a 21*49 22*48
  //   22*47 23*46 24*45 24*44 25*43 25*42 27*41 27*40 28*3f 29*3e 30*3d 32*3c 32*3b 33*3a 34*39 36*38
  //   33*37
  //   contents of rom_1 (hex, n*v repeats v):
  //   20 40 80 c0
endmodule

module Channel_Triangle (
  input  enable,
  input  [7:0] reg10,
  input  [7:0] reg11,
  input  frame_clk
);

  wire buzzer_1_p2;
  wire [13:0] FREQ_q, freq_triangle_data;

  ROM #(.addrWidth(11), .dataWidth(14)) freq_triangle (.addr({reg11[2:0], reg10}), .data(freq_triangle_data));
  Register #(.width(14)) FREQ (.D(freq_triangle_data), .en(1'b1), .clk(frame_clk), .Q(FREQ_q), .clr(1'b0));
  // Buzzer #(.vol_width(4), .waveform("Triangle")) buzzer_1: pin names not known; wires that end beside it: FREQ_q, buzzer_1_p2, 4'b1111
  Register #(.width(1)) ENABLE_R (.D(enable), .en(1'b1), .clk(frame_clk), .Q(buzzer_1_p2), .clr(1'b0));

  // Notes on the sheet:
  //   contents of freq_triangle (hex, n*v repeats v):
  //   3fff 3fff 3fff 369f 2bb2 246a 1f36 1b4f 1846 15d9 13dd 1235 10ce f9b e91 da8 cda c23 b80 aed a67 9ee
  //   980 91a 8bd 867 817 7ce 789 748 70c 6d4 69f 66d 63e 612 5e8 5c0 59a 576 554 534 515 4f7 4db 4c0 4a6
  //   48d 475 45f 449 434 41f 40c 3f9 3e7 3d5 3c4 3b4 3a4 395 386 378 36a 35c 34f 343 337 32b 31f 314 309
  //   2fe 2f4 2ea 2e0 2d6 2cd 2c4 2bb 2b2 2aa 2a2 29a 292 28a 283 27c 274 26d 267 260 259 253 24d 247 241
  //   23b 235 22f 22a 224 21f 21a 215 210 20b 206 201 1fc 1f8 1f3 1ef 1eb 1e6 1e2 1de 1da 1d6 1d2 1ce 1ca
  //   1c7 1c3 1bf 1bc 1b8 1b5 1b2 1ae 1ab 1a8 1a5 1a1 19e 19b 198 195 192 190 18d 18a 187 184 182 17f 17c
  //   17a 177 175 172 170 16e 16b 169 167 164 162 160 15e 15b 159 157 155 153 151 14f 14d 14b 149 147 145
  //   143 141 140 13e 13c 13a 138 137 135 133 132 130 12e 12d 12b 12a 128 126 125 123 122 120 11f 11d 11c
  //   11a 119 118 116 115 114 112 111 110 10e 10d 10c 10a 109 108 107 105 104 103 102 101 ff fe fd fc fb
  //   fa f9 f7 f6 f5 f4 f3 f2 f1 f0 ef ee ed ec eb ea e9 e8 e7 e6 e5 e4 e3 e2 e2 e1 e0 df de dd dc db da
  //   da d9 d8 d7 d6 d5 d5 d4 d3 d2 d1 d1 d0 cf ce ce cd cc cb cb ca c9 c8 c8 c7 c6 c6 c5 c4 c4 c3 c2 c2
  //   c1 c0 c0 bf be be bd bc bc bb ba ba b9 b9 b8 b7 b7 b6 b6 b5 b4 b4 b3 b3 b2 b2 b1 b0 b0 af af ae ae
  //   ad ad ac ac ab ab aa a9 a9 a8 a8 a7 a7 a6 a6 a5 a5 a5 a4 a4 a3 a3 a2 a2 a1 a1 a0 a0 9f 9f 9e 9e 9e
  //   9d 9d 9c 9c 9b 9b 9b 9a 9a 99 99 98 98 98 97 97 96 96 96 95 95 94 94 94 93 93 92 92 92 91 91 91 90
  //   90 8f 8f 8f 8e 8e 8e 8d 8d 8d 8c 8c 8b 8b 8b 8a 8a 8a 89 89 89 88 88 88 87 87 87 86 86 86 4*85 84 84
  //   84 83 83 83 82 82 82 4*81 80 80 80 4*7f 7e 7e 7e 4*7d 7c 7c 7c 4*7b 4*7a 4*79 4*78 77 77 77 5*76
  //   4*75 4*74 4*73 4*72 5*71 4*70 5*6f 4*6e 5*6d 5*6c 5*6b 5*6a 5*69 5*68 5*67 6*66 5*65 6*64 5*63 6*62
  //   6*61 6*60 6*5f 7*5e 6*5d 7*5c 7*5b 6*5a 7*59 8*58 7*57 8*56 7*55 8*54 8*53 9*52 8*51 9*50 9*4f 9*4e
  //   10*4d 9*4c 10*4b 10*4a 11*49 11*48 11*47 11*46 12*45 12*44 13*43 12*42 14*41 13*40 14*3f 15*3e 15*3d
  //   16*3c 16*3b 16*3a 17*39 18*38 19*37 19*36 20*35 21*34 21*33 22*32 24*31 24*30 25*2f 27*2e 27*2d
  //   29*2c 31*2b 31*2a 33*29 35*28 37*27 39*26 41*25 43*24 46*23 48*22 51*21 55*20 58*1f 62*1e 67*1d
  //   71*1c 15*1b
endmodule

module Channel_Noise (
  input  enable,
  input  [7:0] reg12,
  input  [7:0] reg14,
  input  frame_clk
);

  wire buzzer_1_p2;
  wire [3:0] VOL_q;
  wire [13:0] freq_noise_data, FREQ_q;

  ROM #(.addrWidth(4), .dataWidth(14)) freq_noise (.addr(reg14[3:0]), .data(freq_noise_data));
  Register #(.width(4)) VOL (.D(reg12[3:0]), .en(1'b1), .clk(frame_clk), .Q(VOL_q), .clr(1'b0));
  Register #(.width(14)) FREQ (.D(freq_noise_data), .en(1'b1), .clk(frame_clk), .Q(FREQ_q), .clr(1'b0));
  // Buzzer #(.vol_width(4), .waveform("Noise")) buzzer_1: pin names not known; wires that end beside it: FREQ_q, buzzer_1_p2, VOL_q
  Register #(.width(1)) ENABLE_R (.D(enable), .en(1'b1), .clk(frame_clk), .Q(buzzer_1_p2), .clr(1'b0));

  // Notes on the sheet:
  //   contents of freq_noise (hex, n*v repeats v):
  //   c8 b4 a1 91 82 75 69 5e 55 4c 44 3d 37 32 2d 28
endmodule

module APU (
  input  [3:0] ch_mask,
  input  WR,
  input  [3:0] reg_id,
  input  [7:0] value,
  input  frame_clk
);

  wire EN0, EN1, EN2, EN3;
  wire [7:0] reg9_out, regfile_1_reg0_out, regfile_1_reg2_out, regfile_1_reg3_out, regfile_1_reg4_out,
       regfile_1_reg6_out, regfile_1_reg7_out, regfile_1_reg10_out, regfile_1_reg11_out, regfile_1_reg12_out,
       regfile_1_reg14_out;

  RegFile regfile_1 (
    .WR(WR), .reg_id(reg_id), .value(value), .reg0_out(regfile_1_reg0_out), .reg2_out(regfile_1_reg2_out),
    .reg3_out(regfile_1_reg3_out), .reg9_out(reg9_out), .reg12_out(regfile_1_reg12_out),
    .reg4_out(regfile_1_reg4_out), .reg10_out(regfile_1_reg10_out), .reg6_out(regfile_1_reg6_out),
    .reg14_out(regfile_1_reg14_out), .reg11_out(regfile_1_reg11_out), .reg7_out(regfile_1_reg7_out));
  assign {EN3, EN2, EN1, EN0} = reg9_out[3:0] & ch_mask;  // AND_Gate and_1, 4 bits wide
  Channel_Pulse Channel_Pulse1 (
    .enable(EN0), .reg0(regfile_1_reg0_out), .reg2(regfile_1_reg2_out), .reg3(regfile_1_reg3_out),
    .frame_clk(frame_clk));
  Channel_Pulse Channel_Pulse2 (
    .enable(EN1), .reg0(regfile_1_reg4_out), .reg2(regfile_1_reg6_out), .reg3(regfile_1_reg7_out),
    .frame_clk(frame_clk));
  Channel_Triangle channel_triangle_1 (
    .enable(EN2), .reg10(regfile_1_reg10_out), .reg11(regfile_1_reg11_out), .frame_clk(frame_clk));
  Channel_Noise channel_noise_1 (
    .enable(EN3), .reg12(regfile_1_reg12_out), .reg14(regfile_1_reg14_out), .frame_clk(frame_clk));

  // Other names for the same wires on the sheet: FCLK = frame_clk
endmodule
