// Logisim project cpu.circ as structural Verilog
module CPU (
  input  reset,
  input  clk,
  input  start,
  input  en_count
);

  wire AT_ZERO, IS_END, IS_WAIT, IS_WRITE;
  wire [11:0] IMM;
  wire [15:0] bit_extender_1_out, PC_q;
  wire [15:12] INSTR;

  Decoder #(.enable("false"), .select(4)) decoder_1 (
    .out0(IS_WAIT), .out1(IS_WRITE), .out15(IS_END), .sel(INSTR));  // open: out2, out3, out4, out5, out6, out7, out8, out9, out10, out11, out12, out13, out14
  Counter #(.max('hffff), .width(16)) PC (
    .clr(reset), .up(1'b1), .count(1'b1), .clk(clk), .Q(PC_q));  // open: load, D, carry
  ROM #(.addrWidth(16), .dataWidth(16)) rom_1 (.addr(PC_q), .data({INSTR, IMM}));
  assign bit_extender_1_out = {{4{1'b0}}, IMM};  // Bit_Extender bit_extender_1
  Counter #(.max('hffff), .ongoal("stay"), .width(16)) WAITCNT (
    .clr(reset), .load(start), .count(en_count), .clk(clk), .D(bit_extender_1_out), .carry(AT_ZERO));  // open: up, Q

  // Other names for the same wires on the sheet: INSTR[11:0] = IMM; VAL[7:0] = IMM[7:0]; REGID[3:0] = IMM[11:8];
  //   OPCODE[3:0] = INSTR

  // Notes on the sheet:
  //   contents of rom_1 (hex, n*v repeats v):
  //   1b00 1a00 1800 1700 1600 1500 1400 1300 1200 1100 1f00 1e00 1c30 190f 1108 1508 10 1030 143a 1696
  //   1708 1c 1478 1f 14b8 1f 4*20 14b6 1f 6*20 14b5 1f 6*20 14b4 1f 6*20 103a 12bd 1308 14b3 1c 1078 1f
  //   10b8 1f 4*20 10b6 14b2 1e 6*20 10b5 14b1 1e 6*20 10b4 1f 6*20 10b3 1430 1e 6*20 10b2 1f 6*20 10b1 1f
  //   13*20 1030 1f 27*20 1c3c 1e0b 1f08 1d 1c36 1f 1c31 1f 1c30 1f 24*20 1c3c 1f 1c36 1f 1c31 1f 1c30 1f
  //   24*20 1c3c 1f 1c36 1f 1c31 1f 1c30 1f 10*20 143c 161c 1709 1d 143a 160c 1e 16fd 1708 1e 20 20 20
  //   1430 1f 1434 161c 1709 1d 160c 1f 16fd 1708 1e 20 20 20 1430 1f 143c 161c 1709 1c3c 1c 143a 1c36 1e
  //   1c31 1f 1c30 1f 20 20 1430 1f 143c 163f 1e 143a 1f 4*20 1430 1f 143c 16ab 1e 143a 1f 9*20 1693 1f 20
  //   1430 1c31 1e 1077 12bf 130b 143c 167c 18ff 1a3f 1b09 1c3c 17 143a 1adf 1c36 1d 1c31 1f 1c30 1f 10*20
  //   1030 1430 1800 1d 6*20 1434 1f 5*20 1430 1f 1072 143c 161c 18ff 1a3f 1c3c 1a 143a 160c 1adf 1c36 1c
  //   16fd 1708 1800 1c31 1c 1c30 1f 20 20 20 1430 1f 6*20 1077 1434 161c 1709 18ff 1b 160c 1f 16fd 1708
  //   1e 20 20 20 1430 1f 143c 161c 1709 1d 143a 1f 4*20 1030 1800 1e 1077 12f8 1430 18ff 1a52 1c3c 1a
  //   1afb 1c36 1e 1c31 1f 1c30 1f 20 20 20 143c 167c 1e 143a 1f 4*20 1430 1f 1030 143c 1800 1d 143a 1f
  //   4*20 1430 1f 1077 143c 18ff 1d 143a 1f 4*20 1430 1f 1434 1a52 1c3c 1d 1afb 1c36 1e 1c31 1f 1c30 1f
  //   20 20 1430 1f 1030 143c 1800 1d 143a 1f 4*20 1430 1f 1077 12f3 130d 143c 16ab 18ff 1af9 1b0a 18 143a
  //   1f 11*20 1430 1f 1030 143c 167c 1afb 1b09 1c3c 1a 143a 1af9 1b0a 1c36 1c 1800 1c31 1e 1c30 1f 20 20
  //   1430 1f 1434 1f 5*20 1430 1f 1077 143c 18ff 1d 143a 1f 4*20 1430 1f 1434 1f 5*20 1430 1f 1030 143c
  //   161c 1afb 1b09 1c3c 1a 143a 160c 1af9 1b0a 1c36 1b 16fd 1708 1800 1c31 1c 1c30 1f 10*20 1072 1f 16ef
  //   1f 20 20 16fd 1f 20 1430 1f 143c 161c 1709 1d 143a 1f 5*20 1030 1430 18ff 1afb 1b09 1c3c 1a 1af9
  //   1b0a 1c36 1d 1800 1c31 1e 1c30 1f 20 20 20 1434 1f 5*20 1430 1f 1071 143c 162d 1d 143a 161c 1e 160c
  //   1f 20 20 20 1430 1f 1434 1f 5*20 1430 1f 1077 12f8 130b 143c 161c 18ff 1a52 1b09 1c3c 17 143a 1afb
  //   1c36 1d 1c31 1f 1c30 1f 20 20 1430 1f 143c 163f 1e 143a 1f 4*20 1430 1f 143c 1f 143a 1f 11*20 1030
  //   1430 1800 1d 1077 12bf 1434 18ff 1a3f 1c3c 1a 1adf 1c36 1e 1c31 1f 1c30 1f 20 20 1430 1f 143c 16ab
  //   1e 143a 1f 4*20 1430 1f 1030 143c 167c 1800 1c 143a 1f 4*20 1430 1f 1434 1f 5*20 1430 1f 1072 143c
  //   16ab 18ff 1a3f 1c3c 1a 143a 1adf 1c36 1d 1800 1c31 1e 1c30 1f 20 20 1430 1f 143c 167c 1e 143a 1f
  //   4*20 1430 1f 1077 1434 18ff 1d 5*20 1430 1f 143c 161c 1e 143a 1f 4*20 1030 1800 1e 1077 12f8 18ff
  //   1a52 1c3c 1b 1afb 1c36 1e 1c31 1f 1c30 1f 20 20 1430 1f 143c 1f 143a 1f 4*20 1430 1f 1030 143c 160c
  //   1800 1c 143a 1f 4*20 1430 1f 1077 143c 16fd 1708 18ff 1b 143a 1f 4*20 1430 1f 1434 1a52 1c3c 1d 1afb
  //   1c36 1e 1c31 1f 1c30 1f 20 20 1430 1f 1030 143c 16ab 1709 1800 1b 143a 1f 4*20 1430 1f 1077 12f3
  //   130d 143c 18ff 1af9 1b0a 19 143a 1f 4*20 1430 1f 143c 1f 143a 1f 4*20 1430 1f 1030 143c 1afb 1b09
  //   1c3c 1b 143a 1af9 1b0a 1c36 1c 1800 1c31 1e 1c30 1f 20 20 1430 1f 143c 1f 143a 1f 4*20 1430 1f 1077
  //   143c 18ff 1d 143a 1f 4*20 1430 1f 143c 1f 143a 1f 4*20 1430 1f 1030 143c 1afb 1b09 1c3c 1b 143a 1af9
  //   1b0a 1c36 1c 1800 1c31 1e 1c30 1f 9*20 1430 1f 1072 143c 1693 1d 143a 1f 4*20 1430 1f 143c 167c 1e
  //   143a 1f 5*20 1030 1430 18ff 1afb 1b09 1c3c 1a 1af9 1b0a 1c36 1d 1800 1c31 1e 1c30 1f 20 20 20 1434
  //   1f 5*20 1430 1f 1071 143c 161c 1d 143a 160c 1e 16fd 1708 1e 20 20 20 1430 1f 1434 1f 5*20 1430 1f
  //   1077 12f8 130b 143c 161c 1709 18ff 1a52 1b09 1c3c 16 143a 1afb 1c36 1d 1c31 1f 1c30 1f 20 20 1430 1f
  //   143c 163f 1e 143a 1f 4*20 1430 1f 143c 16ab 1e 143a 1f 9*20 1693 1f 20 1030 1430 1800 1d 1077 12bf
  //   143c 167c 18ff 1a3f 1c3c 19 143a 1adf 1c36 1d 1c31 1f 1c30 1f 10*20 1030 1430 1800 1d 6*20 1434 1f
  //   5*20 1430 1f 1072 143c 161c 18ff 1a3f 1c3c 1a 143a 160c 1adf 1c36 1c 16fd 1708 1800 1c31 1c 1c30 1f
  //   20 20 20 1430 1f 6*20 1077 1434 161c 1709 18ff 1b 160c 1f 16fd 1708 1e 20 20 20 1430 1f 143c 161c
  //   1709 1d 143a 1f 4*20 1030 1800 1e 1077 12f8 1430 18ff 1a52 1c3c 1a 1afb 1c36 1e 1c31 1f 1c30 1f 20
  //   20 20 143c 167c 1e 143a 1f 4*20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
endmodule
