// Logisim project cpu_pureAI.circ as structural Verilog: 4 circuits, main circuit main
module main (
  output halt,
  output [15:0] pc_o,
  output [15:0] wait_o,
  output [3:0] reg_o,
  output [7:0] val_o,
  output wr_o,
  output [7:0] r2_o
);

  wire FC_O, mclk;

  Clock clock_1 (.out(mclk));
  CPU cpu_1 (
    .clk(mclk), .reset(1'b0), .tempo_mode(2'b00), .tempo_delta(16'h8), .reg_id(reg_o), .value(val_o),
    .wr(wr_o), .frame_commit(FC_O), .pcout(pc_o), .wait_d(wait_o), .r2_o(r2_o));  // open: r0_o, r1_o, r3_o
  Counter #(.width(8), .max('h60), .ongoal("stay")) tickcnt (
    .clr(1'b0), .load(1'b0), .up(1'b1), .count(1'b1), .clk(mclk), .D({8{1'b0}}), .carry(halt));  // open: Q

  // Other names for the same wires on the sheet: HALTC = halt
endmodule

module play (
  input  reset,
  input  [1:0] tempo
);

  wire AFC, AWR, pclk;
  wire [3:0] AREG;
  wire [7:0] AVAL;

  Clock clock_1 (.out(pclk));
  CPU cpu_1 (
    .clk(pclk), .reset(reset), .tempo_mode(tempo), .tempo_delta(16'h8), .reg_id(AREG), .value(AVAL),
    .wr(AWR), .frame_commit(AFC));  // open: pcout, wait_d, r0_o, r1_o, r2_o, r3_o
  APU apu_1 (.ch_mask(4'b1111), .WR(AWR), .reg_id(AREG), .value(AVAL), .frame_clk(AFC));

  // Other names for the same wires on the sheet: preset = reset; ptmode[1:0] = tempo
endmodule

module CPU (
  input  clk,
  input  reset,
  input  [1:0] tempo_mode,
  input  [15:0] tempo_delta,
  output [3:0] reg_id,
  output [7:0] value,
  output wr,
  output frame_commit,
  output [15:0] pcout,
  output [15:0] wait_d,
  output [7:0] r0_o,
  output [7:0] r1_o,
  output [7:0] r2_o,
  output [7:0] r3_o
);

  wire AT_ZERO, BUSY, BUSYNEXT, CMP_EQ, CMP_LT, ENCOUNT, IMM_LE, IS_ADD, IS_END, IS_LOADI, IS_SUB, IS_WAIT,
       IS_WRITE, IS_WRITEREG, NATZERO, NBUSY, NSTALL, RDOH0, RDOH1, RDOH2, RDOH3, REGWREN, START, WE0, WE1,
       WE2, WE3, WR_EN, WRG1;
  wire [7:0] ALU_ADD, ALU_RES, ALU_SUB, IMM, RA_VAL, RB_VAL, REGWB;
  wire [15:0] ADD_SLOW, FAST_CLAMP, IMM16, SUB_FAST, WAITLOAD;
  wire [15:12] INSTR;

  ROM #(.addrWidth(16), .dataWidth(16)) rom_1 (.addr(pcout), .data({INSTR, reg_id, IMM}));
  Counter #(.width(16), .max('hffff)) PC (
    .clr(reset), .load(IS_END), .up(1'b1), .count(NSTALL), .clk(clk), .D({16{1'b0}}), .Q(pcout));  // open: carry
  assign IMM16 = {{4{1'b0}}, {reg_id, IMM}};  // Bit_Extender bit_extender_1
  Decoder #(.enable("false"), .select(4)) decoder_1 (
    .out0(IS_WAIT), .out1(IS_WRITE), .out4(IS_LOADI), .out5(IS_ADD), .out6(IS_SUB), .out7(IS_WRITEREG),
    .out15(IS_END), .sel(INSTR));  // open: out2, out3, out8, out9, out10, out11, out12, out13, out14
  Counter #(.width(16), .max('hffff), .ongoal("stay")) WAITCNT (
    .clr(reset), .load(START), .up(1'b0), .count(ENCOUNT), .clk(clk), .D(WAITLOAD), .carry(AT_ZERO),
    .Q(wait_d));
  Register #(.width(1)) u_busy (.D(BUSYNEXT), .en(1'b1), .clk(clk), .Q(BUSY), .clr(reset));
  not not_1 (NBUSY, BUSY);
  not not_2 (NATZERO, AT_ZERO);
  not not_3 (NSTALL, BUSYNEXT);
  and and_1 (START, IS_WAIT, NBUSY);
  and and_2 (ENCOUNT, BUSY, NATZERO);
  or or_1 (BUSYNEXT, START, ENCOUNT);
  or or_2 (WR_EN, IS_WRITE, IS_WRITEREG);
  and and_3 (frame_commit, START, clk);
  and and_4 (wr, WR_EN, clk);
  Register #(.width(8)) R0 (.D(REGWB), .en(WE0), .clk(clk), .Q(r0_o), .clr(reset));
  Register #(.width(8)) R1 (.D(REGWB), .en(WE1), .clk(clk), .Q(r1_o), .clr(reset));
  Register #(.width(8)) R2 (.D(REGWB), .en(WE2), .clk(clk), .Q(r2_o), .clr(reset));
  Register #(.width(8)) R3 (.D(REGWB), .en(WE3), .clk(clk), .Q(r3_o), .clr(reset));
  or or_3 (WRG1, IS_LOADI, IS_ADD);
  Adder #(.width(16)) adder_1 (.a(IMM16), .b(tempo_delta), .out(ADD_SLOW), .cin(1'b0));  // open: cout
  Subtractor #(.width(16)) subtractor_1 (.a(IMM16), .b(tempo_delta), .out(SUB_FAST), .bin(1'b0));  // open: bout
  Comparator #(.width(16)) comparator_1 (.a(IMM16), .b(tempo_delta), .eq(CMP_EQ), .lt(CMP_LT));  // open: gt
  or or_4 (REGWREN, WRG1, IS_SUB);
  or or_5 (IMM_LE, CMP_LT, CMP_EQ);
  Multiplexer #(.enable("false"), .select(2), .width(8)) multiplexer_1 (
    .in0(r0_o), .in1(r1_o), .in2(r2_o), .in3(r3_o), .out(RA_VAL), .sel(reg_id[1:0]));
  Multiplexer #(.enable("false"), .select(2), .width(8)) multiplexer_2 (
    .in0(r0_o), .in1(r1_o), .in2(r2_o), .in3(r3_o), .out(RB_VAL), .sel(IMM[7:6]));
  Multiplexer #(.enable("false"), .select(1), .width(16)) multiplexer_3 (
    .in0(SUB_FAST), .in1(16'h1), .out(FAST_CLAMP), .sel(IMM_LE));
  Decoder #(.enable("false"), .select(2)) decoder_2 (
    .out0(RDOH0), .out1(RDOH1), .out2(RDOH2), .out3(RDOH3), .sel(reg_id[3:2]));
  Adder #(.width(8)) adder_2 (.a(RA_VAL), .b(RB_VAL), .out(ALU_ADD), .cin(1'b0));  // open: cout
  Subtractor #(.width(8)) subtractor_2 (.a(RA_VAL), .b(RB_VAL), .out(ALU_SUB), .bin(1'b0));  // open: bout
  Multiplexer #(.enable("false"), .select(2), .width(16)) multiplexer_4 (
    .in0(IMM16), .in1(ADD_SLOW), .in2(FAST_CLAMP), .in3(IMM16), .out(WAITLOAD), .sel(tempo_mode));
  and and_5 (WE0, RDOH0, REGWREN);
  and and_6 (WE1, RDOH1, REGWREN);
  and and_7 (WE2, RDOH2, REGWREN);
  and and_8 (WE3, RDOH3, REGWREN);
  Multiplexer #(.enable("false"), .select(1), .width(8)) multiplexer_5 (
    .in0(ALU_ADD), .in1(ALU_SUB), .out(ALU_RES), .sel(IS_SUB));
  Multiplexer #(.enable("false"), .select(1), .width(8)) multiplexer_6 (
    .in0(ALU_RES), .in1(IMM), .out(REGWB), .sel(IS_LOADI));
  Multiplexer #(.enable("false"), .select(1), .width(8)) multiplexer_7 (
    .in0(IMM), .in1(RB_VAL), .out(value), .sel(IS_WRITEREG));

  // Other names for the same wires on the sheet: FRAMECOMMIT = frame_commit; INSTR[11:0] = {reg_id, IMM};
  //   VAL[7:0] = IMM; VLO[5:0] = IMM[5:0]; RB[1:0] = IMM[7:6]; IMM[11:8] = reg_id; RA[1:0] = reg_id[1:0];
  //   REGID[3:0] = reg_id; RD[1:0] = reg_id[3:2]; OPCODE[3:0] = INSTR; PCQ[15:0] = pcout; R0Q[7:0] = r0_o;
  //   R1Q[7:0] = r1_o; R2Q[7:0] = r2_o; R3Q[7:0] = r3_o; VALUE_OUT[7:0] = value; WCNTQ[15:0] = wait_d; WRPULSE = wr

  // Notes on the sheet:
  //   contents of rom_1 (hex, n*v repeats v):
  //   1b00 1a00 1800 1700 1600 1500 1400 1300 1200 1100 1f00 1e00 1c30 190f 1108 1508 10 1030 143a 1696
  //   1708 1c 1478 1f 14b8 1f 20 20 20 20 14b6 1f 20 20 20 20 20 20 14b5 1f 20 20 20 20 20 20 14b4 1f 20
  //   20 20 20 20 20 103a 12bd 1308 14b3 1c 1078 1f 10b8 1f 20 20 20 20 10b6 14b2 1e 20 20 20 20 20 20
  //   10b5 14b1 1e 20 20 20 20 20 20 10b4 1f 20 20 20 20 20 20 10b3 1430 1e 20 20 20 20 20 20 10b2 1f 20
  //   20 20 20 20 20 10b1 1f 20 20 20 20 20 20 20 20 20 20 20 20 20 1030 1f 20 20 20 20 20 20 20 20 20 20
  //   20 20 20 20 20 20 20 20 20 20 20 20 20 20 20 20 20 1c3c 1e0b 1f08 1d 1c36 1f 1c31 1f 1c30 1f 20 20
  //   20 20 20 20 20 20 20 20 20 20 20 20 20 20 20 20 20 20 20 20 20 20 1c3c 1f 1c36 1f 1c31 1f 1c30 1f 20
  //   20 20 20 20 20 20 20 20 20 20 20 20 20 20 20 20 20 20 20 20 20 20 20 1c3c 1f 1c36 1f 1c31 1f 1c30 1f
  //   20 20 20 20 20 20 20 20 20 20 143c 161c 1709 1d 143a 160c 1e 16fd 1708 1e 20 20 20 1430 1f 1434 161c
  //   1709 1d 160c 1f 16fd 1708 1e 20 20 20 1430 1f 143c 161c 1709 1c3c 1c 143a 1c36 1e 1c31 1f 1c30 1f 20
  //   20 1430 1f 143c 163f 1e 143a 1f 20 20 20 20 1430 1f 143c 16ab 1e 143a 1f 20 20 20 20 20 20 20 20 20
  //   1693 1f 20 1430 1c31 1e 1077 12bf 130b 143c 167c 18ff 1a3f 1b09 1c3c 17 143a 1adf 1c36 1d 1c31 1f
  //   1c30 1f 20 20 20 20 20 20 20 20 20 20 1030 1430 1800 1d 20 20 20 20 20 20 1434 1f 20 20 20 20 20
  //   1430 1f 1072 143c 161c 18ff 1a3f 1c3c 1a 143a 160c 1adf 1c36 1c 16fd 1708 1800 1c31 1c 1c30 1f 20 20
  //   20 1430 1f 20 20 20 20 20 20 1077 1434 161c 1709 18ff 1b 160c 1f 16fd 1708 1e 20 20 20 1430 1f 143c
  //   161c 1709 1d 143a 1f 20 20 20 20 1030 1800 1e 1077 12f8 1430 18ff 1a52 1c3c 1a 1afb 1c36 1e 1c31 1f
  //   1c30 1f 20 20 20 143c 167c 1e 143a 1f 20 20 20 20 1430 1f 1030 143c 1800 1d 143a 1f 20 20 20 20 1430
  //   1f 1077 143c 18ff 1d 143a 1f 20 20 20 20 1430 1f 1434 1a52 1c3c 1d 1afb 1c36 1e 1c31 1f 1c30 1f 20
  //   20 1430 1f 1030 143c 1800 1d 143a 1f 20 20 20 20 1430 1f 1077 12f3 130d 143c 16ab 18ff 1af9 1b0a 18
  //   143a 1f 20 20 20 20 20 20 20 20 20 20 20 1430 1f 1030 143c 167c 1afb 1b09 1c3c 1a 143a 1af9 1b0a
  //   1c36 1c 1800 1c31 1e 1c30 1f 20 20 1430 1f 1434 1f 20 20 20 20 20 1430 1f 1077 143c 18ff 1d 143a 1f
  //   20 20 20 20 1430 1f 1434 1f 20 20 20 20 20 1430 1f 1030 143c 161c 1afb 1b09 1c3c 1a 143a 160c 1af9
  //   1b0a 1c36 1b 16fd 1708 1800 1c31 1c 1c30 1f 20 20 20 20 20 20 20 20 20 20 1072 1f 16ef 1f 20 20 16fd
  //   1f 20 1430 1f 143c 161c 1709 1d 143a 1f 20 20 20 20 20 1030 1430 18ff 1afb 1b09 1c3c 1a 1af9 1b0a
  //   1c36 1d 1800 1c31 1e 1c30 1f 20 20 20 1434 1f 20 20 20 20 20 1430 1f 1071 143c 162d 1d 143a 161c 1e
  //   160c 1f 20 20 20 1430 1f 1434 1f 20 20 20 20 20 1430 1f 1077 12f8 130b 143c 161c 18ff 1a52 1b09 1c3c
  //   17 143a 1afb 1c36 1d 1c31 1f 1c30 1f 20 20 1430 1f 143c 163f 1e 143a 1f 20 20 20 20 1430 1f 143c 1f
  //   143a 1f 20 20 20 20 20 20 20 20 20 20 20 1030 1430 1800 1d 1077 12bf 1434 18ff 1a3f 1c3c 1a 1adf
  //   1c36 1e 1c31 1f 1c30 1f 20 20 1430 1f 143c 16ab 1e 143a 1f 20 20 20 20 1430 1f 1030 143c 167c 1800
  //   1c 143a 1f 20 20 20 20 1430 1f 1434 1f 20 20 20 20 20 1430 1f 1072 143c 16ab 18ff 1a3f 1c3c 1a 143a
  //   1adf 1c36 1d 1800 1c31 1e 1c30 1f 20 20 1430 1f 143c 167c 1e 143a 1f 20 20 20 20 1430 1f 1077 1434
  //   18ff 1d 20 20 20 20 20 1430 1f 143c 161c 1e 143a 1f 20 20 20 20 1030 1800 1e 1077 12f8 18ff 1a52
  //   1c3c 1b 1afb 1c36 1e 1c31 1f 1c30 1f 20 20 1430 1f 143c 1f 143a 1f 20 20 20 20 1430 1f 1030 143c
  //   160c 1800 1c 143a 1f 20 20 20 20 1430 1f 1077 143c 16fd 1708 18ff 1b 143a 1f 20 20 20 20 1430 1f
  //   1434 1a52 1c3c 1d 1afb 1c36 1e 1c31 1f 1c30 1f 20 20 1430 1f 1030 143c 16ab 1709 1800 1b 143a 1f 20
  //   20 20 20 1430 1f 1077 12f3 130d 143c 18ff 1af9 1b0a 19 143a 1f 20 20 20 20 1430 1f 143c 1f 143a 1f
  //   20 20 20 20 1430 1f 1030 143c 1afb 1b09 1c3c 1b 143a 1af9 1b0a 1c36 1c 1800 1c31 1e 1c30 1f 20 20
  //   1430 1f 143c 1f 143a 1f 20 20 20 20 1430 1f 1077 143c 18ff 1d 143a 1f 20 20 20 20 1430 1f 143c 1f
  //   143a 1f 20 20 20 20 1430 1f 1030 143c 1afb 1b09 1c3c 1b 143a 1af9 1b0a 1c36 1c 1800 1c31 1e 1c30 1f
  //   20 20 20 20 20 20 20 20 20 1430 1f 1072 143c 1693 1d 143a 1f 20 20 20 20 1430 1f 143c 167c 1e 143a
  //   1f 20 20 20 20 20 1030 1430 18ff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
endmodule

module CPU_EXT (
  input  clk,
  input  reset,
  input  [1:0] tempo_mode,
  input  [15:0] tempo_delta,
  input  [15:0] instr,
  output [15:0] pcbus,
  output [3:0] reg_id,
  output [7:0] value,
  output wr,
  output frame_commit,
  output [15:0] wait_d
);

  wire AT_ZERO, BUSY, BUSYNEXT, CMP_EQ, CMP_LT, ENCOUNT, IMM_LE, IS_ADD, IS_END, IS_LOADI, IS_SUB, IS_WAIT,
       IS_WRITE, IS_WRITEREG, NATZERO, NBUSY, NSTALL, RDOH0, RDOH1, RDOH2, RDOH3, REGWREN, START, WE0, WE1,
       WE2, WE3, WR_EN, WRG1;
  wire [7:0] ALU_ADD, ALU_RES, ALU_SUB, R0Q, R1Q, R2Q, R3Q, RA_VAL, RB_VAL, REGWB;
  wire [15:0] ADD_SLOW, FAST_CLAMP, IMM16, SUB_FAST, WAITLOAD;

  Counter #(.width(16), .max('hffff)) PC (
    .clr(reset), .load(IS_END), .up(1'b1), .count(NSTALL), .clk(clk), .D({16{1'b0}}), .Q(pcbus));  // open: carry
  assign IMM16 = {{4{1'b0}}, instr[11:0]};  // Bit_Extender bit_extender_1
  Decoder #(.enable("false"), .select(4)) decoder_1 (
    .out0(IS_WAIT), .out1(IS_WRITE), .out4(IS_LOADI), .out5(IS_ADD), .out6(IS_SUB), .out7(IS_WRITEREG),
    .out15(IS_END), .sel(instr[15:12]));  // open: out2, out3, out8, out9, out10, out11, out12, out13, out14
  Counter #(.width(16), .max('hffff), .ongoal("stay")) WAITCNT (
    .clr(reset), .load(START), .up(1'b0), .count(ENCOUNT), .clk(clk), .D(WAITLOAD), .carry(AT_ZERO),
    .Q(wait_d));
  Register #(.width(1)) u_busy (.D(BUSYNEXT), .en(1'b1), .clk(clk), .Q(BUSY), .clr(reset));
  not not_1 (NBUSY, BUSY);
  not not_2 (NATZERO, AT_ZERO);
  not not_3 (NSTALL, BUSYNEXT);
  and and_1 (START, IS_WAIT, NBUSY);
  and and_2 (ENCOUNT, BUSY, NATZERO);
  or or_1 (BUSYNEXT, START, ENCOUNT);
  or or_2 (WR_EN, IS_WRITE, IS_WRITEREG);
  and and_3 (frame_commit, START, clk);
  and and_4 (wr, WR_EN, clk);
  Register #(.width(8)) R0 (.D(REGWB), .en(WE0), .clk(clk), .Q(R0Q), .clr(reset));
  Register #(.width(8)) R1 (.D(REGWB), .en(WE1), .clk(clk), .Q(R1Q), .clr(reset));
  Register #(.width(8)) R2 (.D(REGWB), .en(WE2), .clk(clk), .Q(R2Q), .clr(reset));
  Register #(.width(8)) R3 (.D(REGWB), .en(WE3), .clk(clk), .Q(R3Q), .clr(reset));
  or or_3 (WRG1, IS_LOADI, IS_ADD);
  Adder #(.width(16)) adder_1 (.a(IMM16), .b(tempo_delta), .out(ADD_SLOW), .cin(1'b0));  // open: cout
  Subtractor #(.width(16)) subtractor_1 (.a(IMM16), .b(tempo_delta), .out(SUB_FAST), .bin(1'b0));  // open: bout
  Comparator #(.width(16)) comparator_1 (.a(IMM16), .b(tempo_delta), .eq(CMP_EQ), .lt(CMP_LT));  // open: gt
  or or_4 (REGWREN, WRG1, IS_SUB);
  or or_5 (IMM_LE, CMP_LT, CMP_EQ);
  Multiplexer #(.enable("false"), .select(2), .width(8)) multiplexer_1 (
    .in0(R0Q), .in1(R1Q), .in2(R2Q), .in3(R3Q), .out(RA_VAL), .sel(instr[9:8]));
  Multiplexer #(.enable("false"), .select(2), .width(8)) multiplexer_2 (
    .in0(R0Q), .in1(R1Q), .in2(R2Q), .in3(R3Q), .out(RB_VAL), .sel(instr[7:6]));
  Multiplexer #(.enable("false"), .select(1), .width(16)) multiplexer_3 (
    .in0(SUB_FAST), .in1(16'h1), .out(FAST_CLAMP), .sel(IMM_LE));
  Decoder #(.enable("false"), .select(2)) decoder_2 (
    .out0(RDOH0), .out1(RDOH1), .out2(RDOH2), .out3(RDOH3), .sel(instr[11:10]));
  Adder #(.width(8)) adder_2 (.a(RA_VAL), .b(RB_VAL), .out(ALU_ADD), .cin(1'b0));  // open: cout
  Subtractor #(.width(8)) subtractor_2 (.a(RA_VAL), .b(RB_VAL), .out(ALU_SUB), .bin(1'b0));  // open: bout
  Multiplexer #(.enable("false"), .select(2), .width(16)) multiplexer_4 (
    .in0(IMM16), .in1(ADD_SLOW), .in2(FAST_CLAMP), .in3(IMM16), .out(WAITLOAD), .sel(tempo_mode));
  and and_5 (WE0, RDOH0, REGWREN);
  and and_6 (WE1, RDOH1, REGWREN);
  and and_7 (WE2, RDOH2, REGWREN);
  and and_8 (WE3, RDOH3, REGWREN);
  Multiplexer #(.enable("false"), .select(1), .width(8)) multiplexer_5 (
    .in0(ALU_ADD), .in1(ALU_SUB), .out(ALU_RES), .sel(IS_SUB));
  Multiplexer #(.enable("false"), .select(1), .width(8)) multiplexer_6 (
    .in0(ALU_RES), .in1(instr[7:0]), .out(REGWB), .sel(IS_LOADI));
  Multiplexer #(.enable("false"), .select(1), .width(8)) multiplexer_7 (
    .in0(instr[7:0]), .in1(RB_VAL), .out(value), .sel(IS_WRITEREG));

  assign reg_id = instr[11:8];

  // Other names for the same wires on the sheet: FRAMECOMMIT = frame_commit; IMM[11:0] = instr[11:0];
  //   VAL[7:0] = instr[7:0]; VLO[5:0] = instr[5:0]; RB[1:0] = instr[7:6]; RA[1:0] = instr[9:8];
  //   REGID[3:0] = instr[11:8]; RD[1:0] = instr[11:10]; OPCODE[3:0] = instr[15:12]; PCQ[15:0] = pcbus;
  //   VALUE_OUT[7:0] = value; WCNTQ[15:0] = wait_d; WRPULSE = wr
endmodule
