// Logisim project top_pureAI.circ as structural Verilog: 1 circuit, main circuit main
module main (
  input  run,
  input  reset,
  input  [1:0] tempo,
  input  ch_p1,
  input  ch_p2,
  input  ch_tri,
  input  ch_noise
);

  wire active, AFC, AWR, cpuclk, FCMT, mclk, nactive, NEXTB, nrst, PREVB, ptick, rst, TRKCLK;
  wire [1:0] TRACK;
  wire [3:0] ACH, AREG;
  wire [7:0] AVAL;
  wire [15:0] INSTRBUS, PCADDR, ROM0, ROM1, ROM2, ROM3, WAITDISP;

  Clock clock_1 (.out(mclk));
  Button button_1 (.out(NEXTB));
  Button button_2 (.out(PREVB));
  or or_1 (rst, reset, TRKCLK);
  not not_1 (nrst, reset);
  and and_1 (cpuclk, mclk, run);
  and and_2 (active, run, nrst);
  or or_2 (TRKCLK, NEXTB, PREVB);
  and and_3 (ACH[0], ch_p1, active);
  and and_4 (ACH[1], ch_p2, active);
  and and_5 (ACH[2], ch_tri, active);
  and and_6 (ACH[3], ch_noise, active);
  not not_2 (nactive, active);
  // Probe on TRACK
  Counter #(.max('h3), .width(2)) trkcnt (
    .clr(1'b0), .load(1'b0), .up(NEXTB), .count(1'b1), .clk(TRKCLK), .D(2'b00), .Q(TRACK));  // open: carry
  // Probe on ACH[0]
  // Probe on ACH[1]
  // Probe on ACH[2]
  // Probe on ACH[3]
  and and_7 (ptick, mclk, nactive);
  or or_3 (AFC, FCMT, ptick);
  CPU_EXT cpu_ext_1 (
    .clk(cpuclk), .reset(rst), .tempo_mode(tempo), .tempo_delta(16'h8), .instr(INSTRBUS), .pcbus(PCADDR),
    .reg_id(AREG), .value(AVAL), .wr(AWR), .frame_commit(FCMT), .wait_d(WAITDISP));
  // Probe on PCADDR
  ROM #(.addrWidth(16), .dataWidth(16)) rom_1 (.addr(PCADDR), .data(ROM0));
  ROM #(.addrWidth(16), .dataWidth(16)) rom_2 (.addr(PCADDR), .data(ROM1));
  ROM #(.addrWidth(16), .dataWidth(16)) rom_3 (.addr(PCADDR), .data(ROM2));
  ROM #(.addrWidth(16), .dataWidth(16)) rom_4 (.addr(PCADDR), .data(ROM3));
  Multiplexer #(.select(2), .width(16)) multiplexer_1 (
    .in0(ROM0), .in1(ROM1), .in2(ROM2), .in3(ROM3), .out(INSTRBUS), .sel(TRACK));
  APU apu_1 (.ch_mask(ACH), .WR(AWR), .reg_id(AREG), .value(AVAL), .frame_clk(AFC));

  // Other names for the same wires on the sheet: CH0 = ACH[0]; CH1 = ACH[1]; CH2 = ACH[2]; CH3 = ACH[3]; CH0r = ch_p1;
  //   CH1r = ch_p2; CH2r = ch_tri; CH3r = ch_noise; rst_btn = reset; tmode[1:0] = tempo

  // Notes on the sheet:
  //   ch_p1: initial=0x1
  //   ch_p2: initial=0x1
  //   ch_tri: initial=0x1
  //   ch_noise: initial=0x1
  //   contents of rom_1 (hex, n*v repeats v):
  //   1b00 1a00 1800 1700 1600 1500 1400 1300 1200 1100 1f00 1e00 1c30 190f 1108 1508 10 1030 143a 1696
  //   1708 1c 1478 1f 14b8 1f 4*20 14b6 1f 6*20 14b5 1f 6*20 14b4 1f 6*20 103a 12bd 1308 14b3 1c 1078 1f
  //   10b8 1f 4*20 10b6 14b2 1e 6*20 10b5 14b1 1e 6*20 10b4 1f 6*20 10b3 1430 1e 6*20 10b2 1f 6*20 10b1 1f
  //   13*20 1030 1f 27*20 1c3c 1e0b 1f08 1d 1c36 1f 1c31 1f 1c30 1f 24*20 1c3c 1f 1c36 1f 1c31 1f 1c30 1f
  //   24*20 1c3c 1f 1c36 1f 1c31 1f 1c30 1f 10*20 143c 161c 1709 1d 143a 160c 1e 16fd 1708 1e 20 20 20
  //   1430 1f 1434 161c 1709 1d 160c 1f 16fd 1708 1e 20 20 20 1430 1f 143c 161c 1709 1c3c 1c 143a 1c36 1e
  //   1c31 1f 1c30 1f 20 20 1430 1f 143c 163f 1e 143a 1f 4*20 1430 1f 143c 16ab 1e 143a 1f 9*20 1693 1f 20
  //   1430 1c31 1e 1077 12bf 130b 143c 167c 18ff 1a3f 1b09 1c3c 17 143a 1adf 1c36 1d 1c31 1f 1c30 1f 10*20
  //   1030 1430 1800 1d 6*20 1434 1f 5*20 1430 1f 1072 143c 161c 18ff 1a3f 1c3c 1a 143a 160c 1adf 1c36 1c
  //   16fd 1708 1800 1c31 1c 1c30 1f 20 20 20 1430 1f 6*20 1077 1434 161c 1709 18ff 1b 160c 1f 16fd 1708
  //   1e 20 20 20 1430 1f 143c 161c 1709 1d 143a 1f 4*20 1030 1800 1e 1077 12f8 1430 18ff 1a52 1c3c 1a
  //   1afb 1c36 1e 1c31 1f 1c30 1f 20 20 20 143c 167c 1e 143a 1f 4*20 1430 1f 1030 143c 1800 1d 143a 1f
  //   4*20 1430 1f 1077 143c 18ff 1d 143a 1f 4*20 1430 1f 1434 1a52 1c3c 1d 1afb 1c36 1e 1c31 1f 1c30 1f
  //   20 20 1430 1f 1030 143c 1800 1d 143a 1f 4*20 1430 1f 1077 12f3 130d 143c 16ab 18ff 1af9 1b0a 18 143a
  //   1f 11*20 1430 1f 1030 143c 167c 1afb 1b09 1c3c 1a 143a 1af9 1b0a 1c36 1c 1800 1c31 1e 1c30 1f 20 20
  //   1430 1f 1434 1f 5*20 1430 1f 1077 143c 18ff 1d 143a 1f 4*20 1430 1f 1434 1f 5*20 1430 1f 1030 143c
  //   161c 1afb 1b09 1c3c 1a 143a 160c 1af9 1b0a 1c36 1b 16fd 1708 1800 1c31 1c 1c30 1f 10*20 1072 1f 16ef
  //   1f 20 20 16fd 1f 20 1430 1f 143c 161c 1709 1d 143a 1f 5*20 1030 1430 18ff 1afb 1b09 1c3c 1a 1af9
  //   1b0a 1c36 1d 1800 1c31 1e 1c30 1f 20 20 20 1434 1f 5*20 1430 1f 1071 143c 162d 1d 143a 161c 1e 160c
  //   1f 20 20 20 1430 1f 1434 1f 5*20 1430 1f 1077 12f8 130b 143c 161c 18ff 1a52 1b09 1c3c 17 143a 1afb
  //   1c36 1d 1c31 1f 1c30 1f 20 20 1430 1f 143c 163f 1e 143a 1f 4*20 1430 1f 143c 1f 143a 1f 11*20 1030
  //   1430 1800 1d 1077 12bf 1434 18ff 1a3f 1c3c 1a 1adf 1c36 1e 1c31 1f 1c30 1f 20 20 1430 1f 143c 16ab
  //   1e 143a 1f 4*20 1430 1f 1030 143c 167c 1800 1c 143a 1f 4*20 1430 1f 1434 1f 5*20 1430 1f 1072 143c
  //   16ab 18ff 1a3f 1c3c 1a 143a 1adf 1c36 1d 1800 1c31 1e 1c30 1f 20 20 1430 1f 143c 167c 1e 143a 1f
  //   4*20 1430 1f 1077 1434 18ff 1d 5*20 1430 1f 143c 161c 1e 143a 1f 4*20 1030 1800 1e 1077 12f8 18ff
  //   1a52 1c3c 1b 1afb 1c36 1e 1c31 1f 1c30 1f 20 20 1430 1f 143c 1f 143a 1f 4*20 1430 1f 1030 143c 160c
  //   1800 1c 143a 1f 4*20 1430 1f 1077 143c 16fd 1708 18ff 1b 143a 1f 4*20 1430 1f 1434 1a52 1c3c 1d 1afb
  //   1c36 1e 1c31 1f 1c30 1f 20 20 1430 1f 1030 143c 16ab 1709 1800 1b 143a 1f 4*20 1430 1f 1077 12f3
  //   130d 143c 18ff 1af9 1b0a 19 143a 1f 4*20 1430 1f 143c 1f 143a 1f 4*20 1430 1f 1030 143c 1afb 1b09
  //   1c3c 1b 143a 1af9 1b0a 1c36 1c 1800 1c31 1e 1c30 1f 20 20 1430 1f 143c 1f 143a 1f 4*20 1430 1f 1077
  //   143c 18ff 1d 143a 1f 4*20 1430 1f 143c 1f 143a 1f 4*20 1430 1f 1030 143c 1afb 1b09 1c3c 1b 143a 1af9
  //   1b0a 1c36 1c 1800 1c31 1e 1c30 1f 9*20 1430 1f 1072 143c 1693 1d 143a 1f 4*20 1430 1f 143c 167c 1e
  //   143a 1f 5*20 1030 1430 18ff 1afb 1b09 1c3c 1a 1af9 1b0a 1c36 1d 1800 1c31 1e 1c30 1f 20 20 20 1434
  //   1f 5*20 1430 1f 1071 143c 161c 1d 143a 160c 1e 16fd 1708 1e 20 20 20 1430 1f 1434 1f 5*20 1430 1f
  //   1077 12f8 130b 143c 161c 1709 18ff 1a52 1b09 1c3c 16 143a 1afb 1c36 1d 1c31 1f 1c30 1f 20 20 1430 1f
  //   143c 163f 1e 143a 1f 4*20 1430 1f 143c 16ab 1e 143a 1f 9*20 1693 1f 20 1030 1430 1800 1d 1077 12bf
  //   143c 167c 18ff 1a3f 1c3c 19 143a 1adf 1c36 1d 1c31 1f 1c30 1f 10*20 1030 1430 1800 1d 6*20 1434 1f
  //   5*20 1430 1f 1072 143c 161c 18ff 1a3f 1c3c 1a 143a 160c 1adf 1c36 1c 16fd 1708 1800 1c31 1c 1c30 1f
  //   20 20 20 1430 1f 6*20 1077 1434 161c 1709 18ff 1b 160c 1f 16fd 1708 1e 20 20 20 1430 1f 143c 161c
  //   1709 1d 143a 1f 4*20 1030 1800 1e 1077 12f8 1430 18ff 1a52 1c3c 1a 1afb 1c36 1e 1c31 1f 1c30 1f 20
  //   20 20 143c 167c 1e 143a 1f 4*20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
  //   contents of rom_2 (hex, n*v repeats v):
  //   1b00 1a00 1800 1700 1600 1500 1400 1300 1200 1100 1f00 1e00 1c30 190f 1108 1508 10 1030 1436 16a6
  //   1702 1c 20 1433 1f 20 1034 12fb 1301 1432 1c 20 1032 1434 167c 1701 1c 20 1034 121c 1432 1d 20 1032
  //   127c 1433 16e1 1700 1b 20 121c 16a9 1e 20 127c 16e1 1e 20 121c 16a9 1e 20 127c 16e1 1e 20 121c 16a9
  //   1e 20 127c 16e1 1e 20 121c 16a9 1e 20 127c 16e1 1e 20 121c 16a9 1e 20 127c 16e1 1e 20 1031 121c 1432
  //   16a9 1c 20 127c 16e1 1e 20 121c 16a9 1e 20 127c 16e1 1e 20 121c 16a9 1e 20 127c 16e1 1e 20 121c 16a9
  //   1e 20 127c 16e1 1e 20 121c 1431 16a9 1d 20 127c 16e1 1e 20 121c 16a9 1e 20 127c 16e1 1e 20 121c 16a9
  //   1e 20 127c 16e1 1e 20 121c 16a9 1e 20 127c 16e1 1e 20 121c 16a9 1e 20 127c 16e1 1e 20 121c 16a9 1e
  //   20 127c 16e1 1e 20 121c 16a9 1e 20 127c 16e1 1e 20 121c 16a9 1e 20 127c 16e1 1e 20 121c 16a9 1e 20
  //   127c 16e1 1e 20 121c 16a9 1e 20 127c 16e1 1e 20 121c 16a9 1e 20 127c 16e1 1e 20 121c 16a9 1e 20 127c
  //   16e1 1e 20 1032 12bf 1303 1434 1680 1702 1a 20 12ce 1302 16df 1701 1c 20 12bf 1303 1680 1702 1c 20
  //   12ce 1302 16df 1701 1c 20 12bf 1303 1433 1680 1702 1b 20 12ce 1302 16df 1701 1c 20 12bf 1303 1680
  //   1702 1c 20 12ce 1302 16df 1701 1c 20 12bf 1303 1680 1702 1c 20 12ce 1302 16df 1701 1c 20 12bf 1303
  //   1432 1680 1702 1b 20 12ce 1302 16df 1701 1c 20 1289 1303 1434 165c 1702 1b 20 12a6 1302 16c4 1701 1c
  //   20 1289 1303 165c 1702 1c 20 12a6 1302 16c4 1701 1c 20 1289 1303 1433 165c 1702 1b 20 12a6 1302 16c4
  //   1701 1c 20 1289 1303 1432 165c 1702 1b 20 12a6 1302 16c4 1701 1c 20 1256 1303 1434 163a 1702 1b 20
  //   1280 1302 16ab 1701 1c 20 1256 1303 163a 1702 1c 20 1280 1302 16ab 1701 1c 20 1256 1303 1433 163a
  //   1702 1b 20 1280 1302 16ab 1701 1c 20 1226 1303 1434 161a 1702 1b 20 125c 1302 1693 1701 1c 20 1226
  //   1303 161a 1702 1c 20 125c 1302 1693 1701 1c 20 1226 1303 1433 161a 1702 1b 20 12f9 1302 1434 16fb
  //   1701 1b 20 123a 167c 1e 20 12f9 16fb 1e 20 123a 167c 1e 20 12f9 1433 16fb 1d 20 12ce 1434 16df 1d 20
  //   121a 1667 1e 20 12ce 16df 1e 20 121a 1667 1e 20 12ce 16df 1e 20 121a 1667 1e 20 12a6 16c4 1e 20 12fb
  //   1301 1652 1d 20 12a6 1302 16c4 1d 20 12fb 1301 1652 1d 20 12a6 1302 16c4 1d 20 12fb 1301 1652 1d 20
  //   12a6 1302 1433 16c4 1c 20 12fb 1301 1652 1d 20 12a6 1302 16c4 1d 20 1280 16ab 1e 20 12df 1301 163f
  //   1d 20 1280 1302 16ab 1d 20 12df 1301 163f 1d 20 1280 1302 16ab 1d 20 12df 1301 163f 1d 20 1280 1302
  //   16ab 1d 20 12df 1301 1432 163f 1c 20 1280 1302 16ab 1d 20 12df 1301 163f 1d 20 1280 1302 16ab 1d 20
  //   12df 1301 163f 1d 20 1280 1302 16ab 1d 20 125c 1693 1e 20 12c4 1301 162d 1d 20 125c 1302 1693 1d 20
  //   12c4 1301 162d 1d 20 125c 1302 1693 1d 20 12c4 1301 162d 1d 20 125c 1302 1693 1d 20 12c4 1301 162d
  //   1d 20 1031 125c 1302 1431 1693 1b 20 12c4 1301 162d 1d 20 125c 1302 1693 1d 20 12c4 1301 162d 1d 20
  //   125c 1302 1693 1d 20 12c4 1301 162d 1d 20 125c 1302 1693 1d 20 12c4 1301 162d 1d 20 125c 1302 1693
  //   1d 20 12c4 1301 162d 1d 20 125c 1302 1693 1d 20 12c4 1301 162d 1d 20 125c 1302 1693 1d 20 12c4 1301
  //   162d 1d 20 125c 1302 1693 1d 20 12c4 1301 162d 1d 20 125c 1302 1693 1d 20 12c4 1301 162d 1d 20 125c
  //   1302 1693 1d 20 12c4 1301 162d 1d 20 125c 1302 1693 1d 20 12c4 1301 162d 1d 20 125c 1302 1693 1d 20
  //   12c4 1301 162d 1d 20 125c 1302 1693 1d 20 12c4 1301 162d 1d 20 125c 1302 1693 1d 20 12c4 1301 162d
  //   1d 20 125c 1302 1693 1d 20 12c4 1301 162d 1d 20 125c 1302 1693 1d 20 12c4 1301 162d 1d 20 125c 1302
  //   1693 1d 20 12c4 1301 162d 1d 20 125c 1302 1693 1d 20 12c4 1301 162d 1d 20 125c 1302 1693 1d 20 12c4
  //   1301 162d 1d 20 125c 1302 1693 1d 20 12c4 1301 162d 1d 20 125c 1302 1693 1d 20 12c4 1301 162d 1d 20
  //   125c 1302 1693 1d 20 12c4 1301 162d 1d 20 1030 14f3 1594 16f9 1702 1c34 1e0b 19 20 1c32 1e0d 1e 20
  //   14f1 1c30 1e 14b3 1593 167c 1701 1c34 1e03 1a 20 1c32 1e08 1e 20 1c30 1f 1430 1f 1076 127c 1c33 1e03
  //   1c 20 12f9 1302 1e 1c32 1f 20 1c30 1f 20 20 1030 1f 20 1076 128e 1300 1474 1508 16bd 1700 19 20 121c
  //   1301 167c 1701 1c 4*20 1030 1430 1e 20 1032 12f9 1302 1432 16fb 1b 4*20 1030 1430 1e 20 20 20 1076
  //   129f 1300 1474 16bd 1700 1a 20 123f 1301 167c 1701 1c 4*20 1030 1430 1e 20 1032 121c 1e 20 123a 1302
  //   1e 20 20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
  //   contents of rom_3 (hex, n*v repeats v):
  //   194f 1030 1200 1430 1600 1880 1a00 19 1439 1508 167c 1701 1c 20 1438 1f 20 1437 1f 20 20 20 1439
  //   161c 1e 20 1438 1f 190f 1f 194f 1437 1e 20 20 1439 167c 1e 190f 1f 194f 1438 1e 20 1437 1f 20 20 20
  //   1034 1108 127c 1301 1439 1652 1a 190f 1f 194f 1033 1438 1d 20 1437 1f 20 20 1034 121c 1439 16aa 1c
  //   190f 1f 194f 1033 1438 1d 20 1437 1f 20 20 20 1034 127c 1439 16fb 1c 20 1033 1438 1e 20 1437 1f 20
  //   20 1034 1252 1430 1d 20 1033 1f 20 20 20 20 20 1034 12aa 1439 16fd 1700 1b 20 1033 1438 1e 20 1437
  //   1f 20 20 1034 12fb 1439 16d5 1c 20 1033 1438 1e 20 1437 1f 20 20 20 1030 1439 1652 1701 1c 20 1438
  //   1f 20 1437 1f 20 20 1034 12fd 1300 1439 16e1 1700 1a 20 1033 1438 1e 20 1437 1f 20 20 20 1034 12d5
  //   1439 1652 1701 1b 20 1033 1438 1e 20 1437 1f 20 20 1034 1252 1301 1439 161c 1b 20 1033 1438 1e 20
  //   1437 1f 20 20 20 1034 12e1 1300 1439 16fd 1700 1a 20 1033 1438 1e 20 1437 1f 20 20 1034 1252 1301
  //   1430 1c 20 1033 1f 20 20 20 20 20 1034 121c 1439 1d 20 1033 1438 1e 20 1437 1f 20 20 1034 12fd 1300
  //   1439 167c 1701 1a 20 1033 1438 1e 20 1437 1f 20 20 20 1030 1439 161c 1d 20 1438 1f 20 1437 1f 20 20
  //   1034 1439 167c 1d 20 1033 1438 1e 20 1437 1f 20 20 20 1034 127c 1301 1439 1652 1b 20 1033 1438 1e 20
  //   1437 1f 20 20 1034 121c 1439 16aa 1c 20 1033 1438 1e 20 1437 1f 20 20 20 1034 127c 1439 16fb 1c 20
  //   1033 1438 1e 20 1437 1f 20 20 1034 1252 1430 1d 20 1033 1f 20 20 20 20 20 1034 12aa 1439 16fd 1700
  //   1b 20 1033 1438 1e 20 1437 1f 20 20 1034 12fb 1439 16d5 1c 20 1033 1438 1e 20 1437 1f 20 20 20 1030
  //   1439 1652 1701 1c 20 1438 1f 20 1437 1f 20 20 1034 12fd 1300 1439 16e1 1700 1a 20 1033 1438 1e 20
  //   1437 1f 20 20 20 1034 12d5 1439 1652 1701 1b 20 1033 1438 1e 20 1437 1f 20 20 1034 1252 1301 1439
  //   161c 1b 20 1033 1438 1e 20 1437 1f 20 20 20 1034 12e1 1300 1439 16fd 1700 1a 20 1033 1438 1e 20 1437
  //   1f 20 20 1034 1252 1301 1430 1c 20 1033 1f 20 20 20 20 20 1034 121c 1439 1d 20 1033 1438 1e 20 1437
  //   1f 20 20 10b4 12be 1300 1439 167c 1701 18ff 1aaa 1b01 17 20 10b5 1438 1e 10b6 1f 10b7 1437 1880 1d
  //   20 10b8 1f 20 1439 161c 18ff 1d 20 10b9 1438 1e 20 10ba 1437 1880 1d 20 10bc 1f 1439 167c 1e 20 1438
  //   1f 20 1437 1f 20 20 20 1439 1652 1e 20 1438 1f 20 1437 1f 20 20 1439 16aa 1e 20 1438 1f 20 10bb 1437
  //   1e 20 20 20 1439 16fb 1e 20 1438 1f 20 1437 1f 20 20 1430 18ff 1e 20 20 20 1880 1f 12bd 1f 20 20
  //   1439 16fd 1700 18ff 1c 10ba 1f 1438 1f 12be 1f 1437 1880 1e 20 20 1439 16d5 1e 20 12bd 1438 1e 20
  //   1437 1f 20 20 20 10b9 12be 1439 1652 1701 1b 20 1438 1f 20 10b8 1437 1e 20 12bd 1f 1439 16e1 1700
  //   18ff 1a3a 1b02 1a 20 1438 1f 20 1437 1f 10b7 12be 1e 20 20 1439 1652 1701 1d 10b6 1f 1438 1f 12bd 1f
  //   1437 1f 10b5 1f 20 10b4 128e 1439 161c 1a52 1b01 1a 20 10b5 1438 1e 10b6 1f 10b7 1437 1e 20 10b8 1f
  //   20 1439 16fd 1700 1880 1c 20 10b9 1438 1e 20 10ba 1437 1e 20 10bc 1f 1430 18ff 1a3a 1b02 1c 20 20 20
  //   20 20 20 20 1439 1f 10bb 1f 1438 1f 20 1437 1f 10ba 1f 20 10b4 12a9 1439 167c 1701 1aaa 1b01 19 20
  //   10b5 1438 1e 10b6 1f 10b7 1437 1880 1d 20 10b8 1f 20 1439 161c 18ff 1d 20 10b9 1438 1e 20 10ba 1437
  //   1880 1d 20 10bc 1f 1439 167c 1e 20 1438 1f 20 1437 1f 20 20 20 1439 1652 1e 20 1438 1f 20 1437 1f 20
  //   20 1439 16aa 1e 20 1438 1f 20 10bb 1437 1e 20 20 20 1439 16fb 1e 20 1438 1f 20 1437 1f 20 20 1430
  //   18ff 1e 20 20 20 1880 1f 12a8 1f 20 20 1439 16fd 1700 18ff 1c 10ba 1f 1438 1f 12a9 1f 1437 1880 1e
  //   20 20 1439 16d5 1e 20 12a8 1438 1e 20 1437 1f 20 20 20 10b9 12a9 1439 1652 1701 1b 20 1438 1f 20
  //   10b8 1437 1e 20 12a8 1f 1439 16e1 1700 1d 20 1438 1f 20 1437 1f 10b7 12a9 1e 20 20 1439 1652 1701 1d
  //   10b6 1f 1438 1f 12a8 1f 1437 1f 10b5 1f 20 10b4 12d5 1439 161c 1c 20 10b5 1438 1e 10b6 1f 10b7 1437
  //   1e 20 10b8 1f 20 1439 16fd 1700 1d 20 10b9 1438 1e 20 10ba 1437 1e 20 10bc 1f 1430 1f 20 20 20 20 20
  //   20 20 1439 1f 10bb 1f 1438 1f 20 1437 1f 10ba 1f 20 10b4 12be 1439 167c 1701 18ff 1afb 19 20 10b5
  //   1438 1e 10b6 1f 10b7 1437 1880 1d 20 10b8 1f 20 1439 161c 18ff 1d 20 10b9 1438 1e 20 10ba 1437 1880
  //   1d 20 10bc 1f 1439 167c 1e 20 1438 1f 20 1437 1f 20 20 20 1439 1652 1e 10bb 1f 1438 1f 20 1437 1f
  //   10ba 1f 20 10b4 12a9 1439 16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
  //   contents of rom_4 (hex, n*v repeats v):
  //   1b00 1a00 1800 1700 1600 1500 1400 1300 1200 1100 1f00 1e00 1c30 190f 1108 1508 10 1078 1296 1430 1d
  //   5*20 1072 1f 20 1474 1696 1e 20 20 1078 1277 1e 20 1471 1f 20 20 1072 1f 20 20 1474 1670 1e 20 1078
  //   1270 1c31 1e0a 1c 20 20 1471 1c32 1e09 1d 20 1072 1f 20 20 1474 1664 1c30 1d 20 1078 124b 1c32 1e08
  //   1c 1e07 1f 1e08 1f 1471 1c30 1e 20 20 1072 1c32 1e07 1d 1e06 1f 1474 164b 1c30 1d 20 20 1078 1277
  //   1c32 1e07 1c 1e06 1f 1471 1c30 1e 20 20 1072 1c32 1e07 1d 1e06 1f 1474 1670 1e07 1d 1e06 1f 1e07 1f
  //   1078 1270 1c30 1d 20 20 1471 1f 20 1072 1c32 1e06 1d 1e05 1f 1e06 1f 1474 1664 1c30 1d 20 1078 124b
  //   1c32 1d 1e05 1f 1e06 1f 1471 1e05 1e 1e06 1f 1072 1c30 1e 20 20 1474 164b 1e 20 20 1078 1277 1c32
  //   1e05 1c 1e04 1f 1471 1c30 1e 20 20 1072 1c32 1e05 1d 1e04 1f 1474 1670 1e05 1d 1e04 1f 1e05 1f 1078
  //   1270 1c30 1d 20 1471 1f 20 20 1072 1c32 1e04 1d 1e03 1f 1e04 1f 1474 1664 1c30 1d 20 1078 124b 1c32
  //   1d 1e03 1f 1e04 1f 1471 1e03 1e 1e04 1f 1072 1c30 1e 20 20 1474 164b 1e 20 20 1078 1270 1c32 1e03 1c
  //   1e02 1f 1471 1c30 1e 20 20 1072 1c32 1e03 1d 1e02 1f 1474 1670 1e03 1d 1e02 1f 1e03 1f 1078 124b
  //   1c30 1d 20 1471 1f 20 20 1072 1f 20 20 1474 164b 1e 20 1078 1238 1c32 1e08 1c 1e0d 1f 20 1072 1471
  //   1e08 1d 1e0d 1f 1078 123b 1c33 1d 1e08 1f 1e0d 1f 1072 1474 1638 1d 1e08 1f 1078 1242 1430 1e0d 1c
  //   20 1e08 1f 1072 1474 163b 1e0d 1c 20 1e08 1f 1078 124b 1430 1e0d 1c 20 1072 1474 1642 1e08 1c 1e0d
  //   1f 20 1078 1254 1430 1e07 1c 1e0c 1f 1072 1474 164b 1d 1e07 1f 1e0c 1f 1078 1259 1430 1e05 1c 1e0a
  //   1f 1072 1474 1654 1d 1e05 1f 1e0a 1f 1078 1264 1430 1881 1aab 1b01 1c3b 1e06 18 1adf 1c38 1e02 1d
  //   1a5c 1b02 1e 1072 1474 1659 1af9 1c 1a56 1b03 1e 1078 1270 1430 1abf 1c 1aa6 1b02 1c35 1d 20 1072
  //   1474 1664 1d 20 1471 1c37 1e01 1d 1c36 1e02 1e 1c34 1f 1474 1670 1c32 1d 1c30 1f 1030 1471 1e 5*20
  //   1a52 1b01 1c37 1e01 1c 1c36 1e02 1e 1c34 1f 1c32 1f 1c30 1f 1430 1c37 1e01 1d 1c36 1e02 1e 1c34 1f
  //   1c32 1f 1c30 1f 1074 12a9 1474 16e1 1afd 1b00 1c37 1e08 18 129f 1a0c 1b01 1c34 1e07 1b 1073 1296
  //   1473 1670 1a1c 1e06 1a 1aa6 1b02 1e 124b 16e1 1e 20 1296 1670 1c33 1d 20 124b 16e1 1c32 1d 20 1296
  //   1670 1a52 1b01 1c37 1e01 1a 1c36 1e02 1e 124b 16e1 1c34 1d 1c32 1f 1296 1670 1c30 1d 1072 1472 1c37
  //   1e01 1c 124b 16e1 1c36 1e02 1c 1c34 1f 1296 1670 1c32 1d 1c30 1f 124b 16e1 1e 1aab 1c36 1e06 1d 1296
  //   1670 1adf 1c34 1c 1a5c 1b02 1c33 1e04 1c 124b 16e1 1af9 1c31 1c 1a56 1b03 1c30 1d 1030 1430 1abf 1d
  //   1aa6 1b02 1e 20 20 20 1074 1277 1474 16a9 1a52 1b01 1c37 1e01 18 1270 1c36 1e02 1d 1073 1473 1654
  //   1c34 1c 1238 1c32 1e 16a9 1c30 1e 1270 1c37 1e01 1d 1654 1c36 1e02 1d 1238 1c34 1e 16a9 1c32 1e 1270
  //   1c30 1e 1654 1afd 1b00 1c37 1e08 1b 1238 1a0c 1b01 1c34 1e07 1b 16a9 1a1c 1e06 1d 1270 1aa6 1b02 1d
  //   1654 1f 1072 1238 1472 1d 16a9 1c33 1e 1270 1f 1654 1c32 1e 1238 1f 16a9 1a52 1b01 1c37 1e01 1b 1270
  //   1c36 1e02 1d 1654 1c34 1e 1238 1c32 1e 16a9 1c30 1e 1270 1f 1030 1430 1c37 1e01 1c 1c36 1e02 1e 1c34
  //   1f 1c32 1f 1c30 1f 1074 1277 1474 16c9 1aab 1c36 1e06 19 1adf 1c34 1e 1073 123b 1473 1664 1a5c 1b02
  //   1c33 1e04 18 1af9 1c31 1e 1277 16c9 1a56 1b03 1c30 1b 1abf 1f 123b 1664 1a5c 1b02 1c 20 1277 16c9 1e
  //   20 123b 1664 1a2d 1b01 1c37 1e01 1a 1c36 1e02 1e 1277 16c9 1c34 1d 1c32 1f 123b 1664 1c30 1d 1072
  //   1472 1c37 1e01 1c 1277 16c9 1c36 1e02 1c 1c34 1f 123b 1664 1c32 1d 1c30 1f 1277 16c9 1afd 1b00 1c37
  //   1e08 1a 1a0c 1b01 1c34 1e07 1c 123b 1664 1a1c 1e06 1c 1a5c 1b02 1e 1277 16c9 1e 20 123b 1664 1c33 1d
  //   20 1277 16c9 1c32 1d 20 123b 1664 1c30 1d 1a2d 1b01 1c37 1e01 1c 1277 16c9 1c36 1e02 1c 1c34 1f 123b
  //   1664 1c32 1d 1c30 1f 1030 1430 1c37 1e01 1c 1c36 1e02 1e 1c34 1f 1c32 1f 1c30 1f 1074 125e 1474 1677
  //   1aab 1c36 1e06 19 1259 1adf 1c34 1d 1073 1254 1473 163b 1a5c 1b02 1c33 1e04 18 1af9 1c31 1e 1229
  //   1677 1a56 1b03 1c30 1b 1abf 1f 1254 163b 1a5c 1b02 1c 20 1229 1677 1e 20 1254 163b 1a2d 1b01 1c37
  //   1e01 1a 1c36 1e02 1e 1229 1677 1c34 1d 1c32 1f 1254 163b 1c30 1d 1072 1472 1c37 1e01 1c 1229 1677
  //   1c36 1e02 1c 1c34 1f 1254 163b 1c32 1d 1c30 1f 1229 1677 1e 1074 1264 1474 1afd 1b00 1c37 1e08 19
  //   1a0c 1b01 1c34 1e07 1c 1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
endmodule
