// Logisim project cpu.circ as structural Verilog: 1 circuit, main circuit CPU
module CPU (
  input  clk,
  input  reset,
  input  [1:0] tempo_mode,
  input  [15:0] tempo_delta,
  input  [15:0] instr,
  output [15:0] pcbus,
  output [3:0] reg_id,
  output [7:0] value,
  output wr,
  output frame_commit,
  output [15:0] wait_d
);

  wire AT_ZERO, BUSY, BUSYNEXT, CMP_EQ, CMP_LT, decoder_1_out1, decoder_1_out6, decoder_2_out1, ENCOUNT,
       IMM_LE, IS_ADD, IS_END, IS_LOADI, IS_SUB, IS_WAIT, IS_WRITE, IS_WRITEREG, NATZERO, NBUSY, NSTALL,
       RDOH0, RDOH1, RDOH2, RDOH3, REGWREN, START, WE0, WE1, WE2, WE3, WR_EN, WRG1;
  wire [7:0] ALU_ADD, ALU_RES, ALU_SUB, R0Q, R1Q, R2Q, R3Q, RA_VAL, RB_VAL, REGWB, undriven, undriven_2;
  wire [15:0] ADD_SLOW, FAST_CLAMP, IMM16, SUB_FAST, WAITLOAD;

  Counter #(.max('hffff), .width(16)) PC (
    .clr(reset), .load(IS_END), .up(1'b1), .count(NSTALL), .clk(clk), .D({16{1'b0}}), .Q(pcbus));  // open: carry
  assign IMM16 = {{4{1'b0}}, instr[11:0]};  // Bit_Extender bit_extender_1
  Counter #(.max('hffff), .ongoal("stay"), .width(16)) WAITCNT (
    .clr(reset), .load(START), .up(1'b0), .count(ENCOUNT), .clk(clk), .D(WAITLOAD), .carry(AT_ZERO),
    .Q(wait_d));
  Decoder #(.enable("false"), .select(4)) decoder_1 (
    .out0(IS_WAIT), .out1(decoder_1_out1), .out4(IS_LOADI), .out5(IS_ADD), .out6(decoder_1_out6),
    .out7(IS_WRITEREG), .out15(IS_END), .sel(instr[15:12]));  // open: out2, out3, out8, out9, out10, out11, out12, out13, out14
  Register #(.width(1)) u_busy (.D(BUSYNEXT), .en(1'b1), .clk(clk), .Q(BUSY), .clr(reset));
  not not_1 (NBUSY, BUSY);
  not not_2 (NATZERO, AT_ZERO);
  not not_3 (NSTALL, BUSYNEXT);
  and and_1 (START, IS_WAIT, NBUSY);
  and and_2 (ENCOUNT, BUSY, NATZERO);
  or or_1 (BUSYNEXT, START, ENCOUNT);
  or or_2 (WR_EN, IS_WRITE, IS_WRITEREG);
  and and_3 (frame_commit, START, clk);
  and and_4 (wr, WR_EN, clk);
  or or_3 (WRG1, IS_LOADI, IS_ADD);
  Register R0 (.D(REGWB), .en(WE0), .clk(clk), .Q(R0Q), .clr(reset));
  Register R1 (.D(REGWB), .en(WE1), .clk(clk), .Q(R1Q), .clr(reset));
  Register R2 (.D(REGWB), .en(WE2), .clk(clk), .Q(R2Q), .clr(reset));
  Register R3 (.D(REGWB), .en(WE3), .clk(clk), .Q(R3Q), .clr(reset));
  Adder #(.width(16)) adder_1 (.a(IMM16), .b(tempo_delta), .out(ADD_SLOW), .cin(1'b0));  // open: cout
  Subtractor #(.width(16)) subtractor_1 (.a(IMM16), .b(tempo_delta), .out(SUB_FAST), .bin(1'b0));  // open: bout
  Comparator #(.width(16)) comparator_1 (.a(IMM16), .b(tempo_delta), .eq(CMP_EQ), .lt(CMP_LT));  // open: gt
  or or_4 (REGWREN, WRG1, IS_SUB);
  Decoder #(.enable("false"), .select(2)) decoder_2 (
    .out0(RDOH0), .out1(decoder_2_out1), .out2(RDOH2), .out3(RDOH3), .sel(instr[11:10]));
  Multiplexer #(.select(2), .width(8)) multiplexer_1 (
    .in0(R0Q), .in1(undriven), .in2(R2Q), .in3(R3Q), .out(RA_VAL), .sel(instr[9:8]));
  Multiplexer #(.select(2), .width(8)) multiplexer_2 (
    .in0(R0Q), .in1(R1Q), .in2(undriven_2), .in3(R3Q), .out(RB_VAL), .sel(instr[7:6]));
  or or_5 (IMM_LE, CMP_LT, CMP_EQ);
  Multiplexer #(.width(16)) multiplexer_3 (.in0(SUB_FAST), .in1(16'h1), .out(FAST_CLAMP), .sel(IMM_LE));
  Multiplexer #(.select(2), .width(16)) multiplexer_4 (
    .in0(IMM16), .in1(ADD_SLOW), .in2(FAST_CLAMP), .in3(IMM16), .out(WAITLOAD), .sel(tempo_mode));
  Adder adder_2 (.a(RA_VAL), .b(RB_VAL), .out(ALU_ADD), .cin(1'b0));  // open: cout
  Subtractor subtractor_2 (.a(RA_VAL), .b(RB_VAL), .out(ALU_SUB), .bin(1'b0));  // open: bout
  and and_5 (WE0, RDOH0, REGWREN);
  and and_6 (WE1, RDOH1, REGWREN);
  and and_7 (WE2, RDOH2, REGWREN);
  and and_8 (WE3, RDOH3, REGWREN);
  Multiplexer #(.width(8)) multiplexer_5 (.in0(ALU_ADD), .in1(ALU_SUB), .out(ALU_RES), .sel(IS_SUB));
  Multiplexer #(.width(8)) multiplexer_6 (.in0(ALU_RES), .in1(instr[7:0]), .out(REGWB), .sel(IS_LOADI));
  Multiplexer #(.width(8)) multiplexer_7 (.in0(instr[7:0]), .in1(RB_VAL), .out(value), .sel(IS_WRITEREG));

  assign reg_id = instr[11:8];

  // Other names for the same wires on the sheet: FRAMECOMMIT = frame_commit; IMM[11:0] = instr[11:0];
  //   VAL[7:0] = instr[7:0]; VLO[5:0] = instr[5:0]; RB[1:0] = instr[7:6]; RA[1:0] = instr[9:8];
  //   REGID[3:0] = instr[11:8]; RD[1:0] = instr[11:10]; OPCODE[3:0] = instr[15:12]; PCQ[15:0] = pcbus;
  //   VALUE_OUT[7:0] = value; WCNTQ[15:0] = wait_d; WRPULSE = wr
endmodule
